// Logisim project Лабораторная3.circ as structural Verilog: 17 circuits, main circuit main
module main (
  input  in_1,
  input  in_2,
  output out_3
);

  wire and_1_out, and_2_out, not_1_out, not_2_out;

  not not_1 (not_1_out, in_1);
  and and_1 (and_1_out, not_1_out, in_2);
  and and_2 (and_2_out, in_1, not_2_out);
  not not_2 (not_2_out, in_2);
  or or_1 (out_3, and_1_out, and_2_out);

  // Notes on the sheet:
  //   XOR Circuit
endmodule

module _1_2_o1_min (
  input  a,
  input  b,
  input  c,
  input  d,
  input  e,
  output o1,
  output o2,
  output o3
);

  wire and_1_out, and_2_out, and_3_out, and_4_out, and_5_out, and_6_out, and_7_out, and_8_out, and_9_out,
       and_10_out, and_11_out, and_12_out, and_13_out, and_14_out, and_15_out, and_16_out, and_17_out,
       and_18_out, and_19_out, and_20_out, and_21_out, and_22_out, and_23_out, and_24_out, and_25_out,
       and_26_out, and_27_out, and_28_out, and_29_out, and_30_out, and_31_out, and_32_out, and_33_out,
       and_34_out, and_35_out, and_36_out, not_1_out, not_2_out, not_3_out, not_4_out, not_5_out, not_6_out,
       not_7_out, not_8_out, not_9_out, not_10_out, not_11_out, not_12_out, not_13_out, not_14_out,
       not_15_out, not_16_out, not_17_out, not_18_out, not_19_out, not_20_out, not_21_out, not_22_out,
       not_23_out, not_24_out, not_25_out, not_26_out, not_27_out, not_28_out, not_29_out, not_30_out,
       not_31_out, not_32_out, not_33_out, not_34_out, not_35_out, not_36_out, not_37_out, not_38_out,
       not_39_out, not_40_out, not_41_out, not_42_out, not_43_out, not_44_out, not_45_out, not_46_out,
       not_47_out, not_48_out, not_49_out, not_50_out, not_51_out, not_52_out, not_53_out, not_54_out,
       not_55_out, not_56_out, not_57_out, not_58_out, not_59_out, not_60_out;

  and and_1 (and_1_out, d, e);
  and and_2 (and_2_out, c, e);
  and and_3 (and_3_out, c, d);
  and and_4 (and_4_out, b, e);
  and and_5 (and_5_out, b, d);
  and and_6 (and_6_out, b, c);
  and and_7 (and_7_out, a, e);
  and and_8 (and_8_out, a, d);
  and and_9 (and_9_out, a, c);
  and and_10 (and_10_out, a, b);
  not not_1 (not_1_out, a);
  not not_2 (not_2_out, b);
  not not_3 (not_3_out, c);
  not not_4 (not_4_out, d);
  not not_5 (not_5_out, a);
  not not_6 (not_6_out, b);
  not not_7 (not_7_out, c);
  not not_8 (not_8_out, e);
  not not_9 (not_9_out, a);
  not not_10 (not_10_out, b);
  not not_11 (not_11_out, d);
  not not_12 (not_12_out, e);
  not not_13 (not_13_out, a);
  not not_14 (not_14_out, c);
  not not_15 (not_15_out, d);
  not not_16 (not_16_out, e);
  not not_17 (not_17_out, b);
  not not_18 (not_18_out, c);
  not not_19 (not_19_out, d);
  not not_20 (not_20_out, e);
  not not_21 (not_21_out, a);
  not not_22 (not_22_out, b);
  not not_23 (not_23_out, c);
  not not_24 (not_24_out, d);
  not not_25 (not_25_out, a);
  not not_26 (not_26_out, b);
  not not_27 (not_27_out, c);
  not not_28 (not_28_out, e);
  not not_29 (not_29_out, a);
  not not_30 (not_30_out, b);
  not not_31 (not_31_out, d);
  not not_32 (not_32_out, e);
  not not_33 (not_33_out, a);
  not not_34 (not_34_out, b);
  not not_35 (not_35_out, a);
  not not_36 (not_36_out, c);
  not not_37 (not_37_out, d);
  not not_38 (not_38_out, e);
  not not_39 (not_39_out, a);
  not not_40 (not_40_out, c);
  not not_41 (not_41_out, a);
  not not_42 (not_42_out, d);
  not not_43 (not_43_out, a);
  not not_44 (not_44_out, e);
  not not_45 (not_45_out, b);
  not not_46 (not_46_out, c);
  not not_47 (not_47_out, d);
  not not_48 (not_48_out, e);
  not not_49 (not_49_out, b);
  not not_50 (not_50_out, c);
  not not_51 (not_51_out, b);
  not not_52 (not_52_out, d);
  not not_53 (not_53_out, b);
  not not_54 (not_54_out, e);
  not not_55 (not_55_out, c);
  not not_56 (not_56_out, d);
  not not_57 (not_57_out, c);
  not not_58 (not_58_out, e);
  not not_59 (not_59_out, d);
  not not_60 (not_60_out, e);
  or or_1 (o1, and_1_out, and_2_out, and_3_out, and_4_out, and_5_out, and_6_out, and_7_out, and_8_out, and_9_out, and_10_out);
  and and_11 (and_11_out, not_1_out, not_2_out, not_3_out, not_4_out);
  and and_12 (and_12_out, not_5_out, not_6_out, not_7_out, not_8_out);
  and and_13 (and_13_out, not_9_out, not_10_out, not_11_out, not_12_out);
  and and_14 (and_14_out, not_13_out, not_14_out, not_15_out, not_16_out);
  and and_15 (and_15_out, not_17_out, not_18_out, not_19_out, not_20_out);
  and and_16 (and_16_out, b, c, d, e);
  and and_17 (and_17_out, a, c, d, e);
  and and_18 (and_18_out, a, b, d, e);
  and and_19 (and_19_out, a, b, c, e);
  and and_20 (and_20_out, a, b, c, d);
  and and_21 (and_21_out, not_21_out, not_22_out, not_23_out, not_24_out, e);
  and and_22 (and_22_out, not_25_out, not_26_out, not_27_out, d, not_28_out);
  and and_23 (and_23_out, not_29_out, not_30_out, c, not_31_out, not_32_out);
  and and_24 (and_24_out, not_33_out, not_34_out, c, d, e);
  and and_25 (and_25_out, not_35_out, b, not_36_out, not_37_out, not_38_out);
  and and_26 (and_26_out, not_39_out, b, not_40_out, d, e);
  and and_27 (and_27_out, not_41_out, b, c, not_42_out, e);
  and and_28 (and_28_out, not_43_out, b, c, d, not_44_out);
  and and_29 (and_29_out, a, not_45_out, not_46_out, not_47_out, not_48_out);
  and and_30 (and_30_out, a, not_49_out, not_50_out, d, e);
  and and_31 (and_31_out, a, not_51_out, c, not_52_out, e);
  and and_32 (and_32_out, a, not_53_out, c, d, not_54_out);
  and and_33 (and_33_out, a, b, not_55_out, not_56_out, e);
  and and_34 (and_34_out, a, b, not_57_out, d, not_58_out);
  and and_35 (and_35_out, a, b, c, not_59_out, not_60_out);
  and and_36 (and_36_out, a, b, c, d, e);
  or or_2 (o2, and_11_out, and_12_out, and_13_out, and_14_out, and_15_out, and_16_out, and_17_out, and_18_out, and_19_out, and_20_out);
  or or_3 (o3, and_21_out, and_22_out, and_23_out, and_24_out, and_25_out, and_26_out, and_27_out, and_28_out, and_29_out, and_30_out, and_31_out, and_32_out, and_33_out, and_34_out, and_35_out, and_36_out);
endmodule

module \_1_2_о2_min  (
  input  a,
  input  b,
  input  c,
  input  d,
  input  e,
  output o1,
  output o2,
  output o3
);

  wire and_1_out, and_2_out, and_3_out, and_4_out, and_5_out, and_6_out, and_7_out, and_8_out, and_9_out,
       and_10_out, and_11_out, and_12_out, and_13_out, and_14_out, and_15_out, and_16_out, and_17_out,
       and_18_out, and_19_out, and_20_out, and_21_out, and_22_out, and_23_out, and_24_out, and_25_out,
       and_26_out, not_1_out, not_2_out, not_3_out, not_4_out, not_5_out, not_6_out, not_7_out, not_8_out,
       not_9_out, not_10_out, not_11_out, not_12_out, not_13_out, not_14_out, not_15_out, not_16_out,
       not_17_out, not_18_out, not_19_out, not_20_out, not_21_out, not_22_out, not_23_out, not_24_out,
       not_25_out, not_26_out, not_27_out, not_28_out, not_29_out, not_30_out, not_31_out, not_32_out,
       not_33_out, not_34_out, not_35_out, not_36_out, not_37_out, not_38_out, not_39_out, not_40_out,
       not_41_out, not_42_out, not_43_out, not_44_out, not_45_out, not_46_out, not_47_out, not_48_out,
       not_49_out, not_50_out, not_51_out, not_52_out, not_53_out, not_54_out, not_55_out, not_56_out,
       not_57_out, not_58_out, not_59_out, not_60_out, not_61_out, not_62_out, not_63_out, not_64_out,
       not_65_out, not_66_out, not_67_out, not_68_out, or_2_out, or_3_out, or_4_out, or_5_out, or_6_out,
       or_7_out, or_8_out, or_9_out, or_10_out, or_11_out, or_12_out, or_13_out, or_14_out, or_15_out;

  and and_1 (and_1_out, d, e);
  and and_2 (and_2_out, c, e);
  and and_3 (and_3_out, c, d);
  and and_4 (and_4_out, b, e);
  and and_5 (and_5_out, b, d);
  and and_6 (and_6_out, b, c);
  and and_7 (and_7_out, a, e);
  and and_8 (and_8_out, a, d);
  and and_9 (and_9_out, a, c);
  and and_10 (and_10_out, a, b);
  not not_1 (not_1_out, d);
  not not_2 (not_2_out, e);
  not not_3 (not_3_out, c);
  not not_4 (not_4_out, e);
  not not_5 (not_5_out, c);
  not not_6 (not_6_out, d);
  not not_7 (not_7_out, b);
  not not_8 (not_8_out, e);
  not not_9 (not_9_out, b);
  not not_10 (not_10_out, d);
  not not_11 (not_11_out, b);
  not not_12 (not_12_out, c);
  not not_13 (not_13_out, b);
  not not_14 (not_14_out, c);
  not not_15 (not_15_out, a);
  not not_16 (not_16_out, e);
  not not_17 (not_17_out, a);
  not not_18 (not_18_out, d);
  not not_19 (not_19_out, a);
  not not_20 (not_20_out, c);
  not not_21 (not_21_out, a);
  not not_22 (not_22_out, c);
  not not_23 (not_23_out, a);
  not not_24 (not_24_out, b);
  not not_25 (not_25_out, a);
  not not_26 (not_26_out, b);
  not not_27 (not_27_out, a);
  not not_28 (not_28_out, b);
  not not_29 (not_29_out, a);
  not not_30 (not_30_out, b);
  not not_31 (not_31_out, c);
  not not_32 (not_32_out, d);
  not not_33 (not_33_out, a);
  not not_34 (not_34_out, b);
  not not_35 (not_35_out, c);
  not not_36 (not_36_out, e);
  not not_37 (not_37_out, a);
  not not_38 (not_38_out, b);
  not not_39 (not_39_out, d);
  not not_40 (not_40_out, e);
  not not_41 (not_41_out, a);
  not not_42 (not_42_out, b);
  not not_43 (not_43_out, a);
  not not_44 (not_44_out, c);
  not not_45 (not_45_out, d);
  not not_46 (not_46_out, e);
  not not_47 (not_47_out, a);
  not not_48 (not_48_out, c);
  not not_49 (not_49_out, a);
  not not_50 (not_50_out, d);
  not not_51 (not_51_out, a);
  not not_52 (not_52_out, e);
  not not_53 (not_53_out, b);
  not not_54 (not_54_out, c);
  not not_55 (not_55_out, d);
  not not_56 (not_56_out, e);
  not not_57 (not_57_out, b);
  not not_58 (not_58_out, c);
  not not_59 (not_59_out, b);
  not not_60 (not_60_out, d);
  not not_61 (not_61_out, b);
  not not_62 (not_62_out, e);
  not not_63 (not_63_out, c);
  not not_64 (not_64_out, d);
  not not_65 (not_65_out, c);
  not not_66 (not_66_out, e);
  not not_67 (not_67_out, d);
  not not_68 (not_68_out, e);
  or or_1 (o1, and_1_out, and_2_out, and_3_out, and_4_out, and_5_out, and_6_out, and_7_out, and_8_out, and_9_out, and_10_out);
  or or_2 (or_2_out, a, b, not_1_out, not_2_out);
  or or_3 (or_3_out, a, b, not_3_out, not_4_out);
  or or_4 (or_4_out, a, b, not_5_out, not_6_out);
  or or_5 (or_5_out, a, not_7_out, c, not_8_out);
  or or_6 (or_6_out, a, not_9_out, c, not_10_out);
  or or_7 (or_7_out, a, not_11_out, not_12_out, d);
  or or_8 (or_8_out, a, not_13_out, not_14_out, e);
  or or_9 (or_9_out, not_15_out, b, c, not_16_out);
  or or_10 (or_10_out, not_17_out, b, c, not_18_out);
  or or_11 (or_11_out, not_19_out, b, not_20_out, d);
  or or_12 (or_12_out, not_21_out, b, not_22_out, e);
  or or_13 (or_13_out, not_23_out, not_24_out, c, d);
  or or_14 (or_14_out, not_25_out, not_26_out, c, e);
  or or_15 (or_15_out, not_27_out, not_28_out, d, e);
  and and_11 (and_11_out, not_29_out, not_30_out, not_31_out, not_32_out, e);
  and and_12 (and_12_out, not_33_out, not_34_out, not_35_out, d, not_36_out);
  and and_13 (and_13_out, not_37_out, not_38_out, c, not_39_out, not_40_out);
  and and_14 (and_14_out, not_41_out, not_42_out, c, d, e);
  and and_15 (and_15_out, not_43_out, b, not_44_out, not_45_out, not_46_out);
  and and_16 (and_16_out, not_47_out, b, not_48_out, d, e);
  and and_17 (and_17_out, not_49_out, b, c, not_50_out, e);
  and and_18 (and_18_out, not_51_out, b, c, d, not_52_out);
  and and_19 (and_19_out, a, not_53_out, not_54_out, not_55_out, not_56_out);
  and and_20 (and_20_out, a, not_57_out, not_58_out, d, e);
  and and_21 (and_21_out, a, not_59_out, c, not_60_out, e);
  and and_22 (and_22_out, a, not_61_out, c, d, not_62_out);
  and and_23 (and_23_out, a, b, not_63_out, not_64_out, e);
  and and_24 (and_24_out, a, b, not_65_out, d, not_66_out);
  and and_25 (and_25_out, a, b, c, not_67_out, not_68_out);
  and and_26 (and_26_out, a, b, c, d, e);
  and and_27 (o2, or_2_out, or_3_out, or_4_out, or_5_out, or_6_out, or_7_out, or_8_out, or_9_out, or_10_out, or_11_out, or_12_out, or_13_out, or_14_out, or_15_out);
  or or_16 (o3, and_11_out, and_12_out, and_13_out, and_14_out, and_15_out, and_16_out, and_17_out, and_18_out, and_19_out, and_20_out, and_21_out, and_22_out, and_23_out, and_24_out, and_25_out, and_26_out);
endmodule

module _1_2_o3_min (
  input  a,
  input  b,
  input  c,
  input  d,
  input  e,
  output o1,
  output o2,
  output o3
);

  wire and_1_out, and_2_out, and_3_out, and_4_out, and_5_out, and_6_out, and_7_out, and_8_out, and_9_out,
       and_10_out, and_11_out, and_12_out, and_13_out, and_14_out, and_15_out, and_16_out, and_17_out,
       and_18_out, and_19_out, and_20_out, and_21_out, and_22_out, and_23_out, and_24_out, and_25_out,
       and_26_out, and_27_out, and_28_out, and_29_out, and_30_out, and_31_out, and_32_out, and_33_out,
       and_34_out, and_36_out, and_37_out, not_1_out, not_2_out, not_3_out, not_4_out, not_5_out, not_6_out,
       not_7_out, not_8_out, not_9_out, not_10_out, not_11_out, not_12_out, not_13_out, not_14_out,
       not_15_out, not_16_out, not_17_out, not_18_out, not_19_out, not_20_out, not_21_out, not_22_out,
       not_23_out, not_24_out, not_25_out, not_26_out, not_27_out, not_28_out, not_29_out, not_30_out,
       not_31_out, not_32_out, not_33_out, not_34_out, not_35_out, not_36_out, not_37_out, not_38_out,
       not_39_out, not_40_out, not_41_out, not_42_out, not_43_out, not_44_out, not_45_out, not_46_out,
       not_47_out, not_48_out, not_49_out, not_50_out, not_51_out, not_52_out, not_53_out, not_54_out,
       not_55_out, not_56_out, not_57_out, not_58_out, not_59_out, not_60_out, not_61_out, not_62_out,
       not_63_out, not_64_out, not_65_out, not_66_out, not_67_out, not_68_out, or_1_out, or_2_out, or_3_out,
       or_4_out, or_5_out, or_6_out, or_7_out, or_8_out, or_9_out, or_10_out, or_11_out, or_12_out,
       or_13_out, or_14_out, or_15_out, or_16_out, or_17_out, or_18_out, or_19_out, or_20_out, or_21_out,
       or_22_out, or_23_out, or_24_out, or_25_out, or_26_out, or_27_out, or_28_out, or_29_out, or_30_out,
       or_31_out, or_32_out, or_33_out, or_34_out, or_35_out, or_36_out, or_37_out, or_38_out, or_39_out,
       or_40_out, or_41_out, or_42_out, or_43_out, or_44_out, or_45_out, or_46_out, or_47_out, or_48_out,
       or_49_out, or_50_out, or_51_out, or_52_out, or_53_out, or_54_out, or_55_out, or_56_out, or_57_out,
       or_58_out, or_59_out, or_60_out, or_61_out, or_62_out, or_63_out, or_64_out, or_65_out, or_66_out,
       or_67_out, or_68_out, or_69_out, or_70_out, or_71_out, or_72_out, or_73_out, or_74_out, or_75_out,
       or_76_out, or_77_out, or_78_out, or_79_out, or_80_out, or_81_out, or_82_out, or_83_out, or_84_out,
       or_85_out, or_86_out, or_87_out, or_88_out, or_89_out, or_90_out, or_91_out, or_92_out, or_93_out,
       or_94_out, or_95_out, or_96_out, or_97_out, or_98_out, or_99_out, or_100_out, or_101_out, or_102_out,
       or_103_out, or_104_out, or_105_out, or_106_out, or_107_out, or_108_out, or_109_out, or_110_out,
       or_111_out, or_112_out, or_113_out, or_115_out;

  and and_1 (and_1_out, d, e);
  and and_2 (and_2_out, c, e);
  and and_3 (and_3_out, b, c);
  and and_4 (and_4_out, a, e);
  not not_1 (not_1_out, d);
  not not_2 (not_2_out, e);
  not not_3 (not_3_out, c);
  not not_4 (not_4_out, e);
  not not_5 (not_5_out, c);
  not not_6 (not_6_out, d);
  not not_7 (not_7_out, b);
  not not_8 (not_8_out, e);
  not not_9 (not_9_out, b);
  not not_10 (not_10_out, d);
  not not_11 (not_11_out, b);
  not not_12 (not_12_out, c);
  not not_13 (not_13_out, a);
  not not_14 (not_14_out, e);
  not not_15 (not_15_out, a);
  not not_16 (not_16_out, d);
  not not_17 (not_17_out, a);
  not not_18 (not_18_out, c);
  not not_19 (not_19_out, a);
  not not_20 (not_20_out, c);
  not not_21 (not_21_out, a);
  not not_22 (not_22_out, b);
  not not_23 (not_23_out, a);
  not not_24 (not_24_out, b);
  not not_25 (not_25_out, b);
  not not_26 (not_26_out, b);
  not not_27 (not_27_out, b);
  not not_28 (not_28_out, b);
  not not_29 (not_29_out, a);
  not not_30 (not_30_out, a);
  not not_31 (not_31_out, a);
  not not_32 (not_32_out, a);
  not not_33 (not_33_out, a);
  not not_34 (not_34_out, b);
  not not_35 (not_35_out, a);
  not not_36 (not_36_out, b);
  not not_37 (not_37_out, a);
  not not_38 (not_38_out, b);
  not not_39 (not_39_out, a);
  not not_40 (not_40_out, b);
  or or_1 (or_1_out, and_1_out, and_2_out);
  and and_5 (and_5_out, c, d);
  and and_6 (and_6_out, b, e);
  and and_7 (and_7_out, b, d);
  or or_2 (or_2_out, and_3_out, and_4_out);
  and and_8 (and_8_out, a, d);
  and and_9 (and_9_out, a, c);
  and and_10 (and_10_out, a, b);
  or or_3 (or_3_out, a, b);
  or or_4 (or_4_out, not_1_out, not_2_out);
  or or_5 (or_5_out, a, b);
  or or_6 (or_6_out, not_3_out, not_4_out);
  or or_7 (or_7_out, a, b);
  or or_8 (or_8_out, not_5_out, not_6_out);
  or or_9 (or_9_out, a, not_7_out);
  or or_10 (or_10_out, c, not_8_out);
  or or_11 (or_11_out, a, not_9_out);
  or or_12 (or_12_out, c, not_10_out);
  or or_13 (or_13_out, a, not_11_out);
  or or_14 (or_14_out, not_12_out, d);
  not not_41 (not_41_out, b);
  not not_42 (not_42_out, c);
  or or_15 (or_15_out, not_13_out, b);
  or or_16 (or_16_out, c, not_14_out);
  or or_17 (or_17_out, not_15_out, b);
  or or_18 (or_18_out, c, not_16_out);
  or or_19 (or_19_out, not_17_out, b);
  or or_20 (or_20_out, not_18_out, d);
  or or_21 (or_21_out, not_19_out, b);
  or or_22 (or_22_out, not_20_out, e);
  or or_23 (or_23_out, not_21_out, not_22_out);
  or or_24 (or_24_out, c, d);
  or or_25 (or_25_out, not_23_out, not_24_out);
  or or_26 (or_26_out, c, e);
  not not_43 (not_43_out, a);
  not not_44 (not_44_out, b);
  or or_27 (or_27_out, a, b);
  or or_28 (or_28_out, a, b);
  not not_45 (not_45_out, d);
  not not_46 (not_46_out, e);
  or or_29 (or_29_out, a, b);
  not not_47 (not_47_out, c);
  not not_48 (not_48_out, e);
  or or_30 (or_30_out, a, b);
  not not_49 (not_49_out, c);
  not not_50 (not_50_out, d);
  or or_31 (or_31_out, a, not_25_out);
  not not_51 (not_51_out, e);
  or or_32 (or_32_out, a, not_26_out);
  not not_52 (not_52_out, d);
  or or_33 (or_33_out, a, not_27_out);
  not not_53 (not_53_out, c);
  or or_34 (or_34_out, a, not_28_out);
  not not_54 (not_54_out, c);
  not not_55 (not_55_out, d);
  not not_56 (not_56_out, e);
  or or_35 (or_35_out, not_29_out, b);
  not not_57 (not_57_out, e);
  or or_36 (or_36_out, not_30_out, b);
  not not_58 (not_58_out, d);
  or or_37 (or_37_out, not_31_out, b);
  not not_59 (not_59_out, c);
  or or_38 (or_38_out, not_32_out, b);
  not not_60 (not_60_out, c);
  not not_61 (not_61_out, d);
  not not_62 (not_62_out, e);
  or or_39 (or_39_out, not_33_out, not_34_out);
  or or_40 (or_40_out, not_35_out, not_36_out);
  not not_63 (not_63_out, d);
  not not_64 (not_64_out, e);
  or or_41 (or_41_out, not_37_out, not_38_out);
  not not_65 (not_65_out, c);
  not not_66 (not_66_out, e);
  or or_42 (or_42_out, not_39_out, not_40_out);
  not not_67 (not_67_out, c);
  not not_68 (not_68_out, d);
  or or_43 (or_43_out, or_1_out, and_5_out);
  or or_44 (or_44_out, and_6_out, and_7_out);
  or or_45 (or_45_out, or_2_out, and_8_out);
  or or_46 (or_46_out, and_9_out, and_10_out);
  or or_47 (or_47_out, or_3_out, or_4_out);
  and and_11 (and_11_out, or_47_out, or_48_out);
  or or_48 (or_48_out, or_5_out, or_6_out);
  or or_49 (or_49_out, or_7_out, or_8_out);
  and and_12 (and_12_out, or_49_out, or_50_out);
  or or_50 (or_50_out, or_9_out, or_10_out);
  or or_51 (or_51_out, or_11_out, or_12_out);
  and and_13 (and_13_out, or_51_out, or_52_out);
  or or_52 (or_52_out, or_13_out, or_14_out);
  or or_53 (or_53_out, a, not_41_out);
  or or_54 (or_54_out, or_53_out, or_55_out);
  or or_55 (or_55_out, not_42_out, e);
  or or_56 (or_56_out, or_15_out, or_16_out);
  and and_14 (and_14_out, or_56_out, or_57_out);
  or or_57 (or_57_out, or_17_out, or_18_out);
  or or_58 (or_58_out, or_19_out, or_20_out);
  and and_15 (and_15_out, or_58_out, or_59_out);
  or or_59 (or_59_out, or_21_out, or_22_out);
  or or_60 (or_60_out, or_23_out, or_24_out);
  and and_16 (and_16_out, or_60_out, or_61_out);
  or or_61 (or_61_out, or_25_out, or_26_out);
  or or_62 (or_62_out, not_43_out, not_44_out);
  or or_63 (or_63_out, or_62_out, or_64_out);
  or or_64 (or_64_out, d, e);
  or or_65 (or_65_out, or_27_out, c);
  or or_66 (or_66_out, or_65_out, or_67_out);
  or or_67 (or_67_out, d, e);
  or or_68 (or_68_out, or_28_out, c);
  or or_69 (or_69_out, or_68_out, or_70_out);
  or or_70 (or_70_out, not_45_out, not_46_out);
  or or_71 (or_71_out, or_29_out, not_47_out);
  or or_72 (or_72_out, or_71_out, or_73_out);
  or or_73 (or_73_out, d, not_48_out);
  or or_74 (or_74_out, or_30_out, not_49_out);
  or or_75 (or_75_out, or_74_out, or_76_out);
  or or_76 (or_76_out, not_50_out, e);
  or or_77 (or_77_out, or_31_out, c);
  or or_78 (or_78_out, or_77_out, or_79_out);
  or or_79 (or_79_out, d, not_51_out);
  or or_80 (or_80_out, or_32_out, c);
  or or_81 (or_81_out, or_80_out, or_82_out);
  or or_82 (or_82_out, not_52_out, e);
  or or_83 (or_83_out, or_33_out, not_53_out);
  or or_84 (or_84_out, or_83_out, or_85_out);
  or or_85 (or_85_out, d, e);
  or or_86 (or_86_out, or_34_out, not_54_out);
  or or_87 (or_87_out, or_86_out, or_88_out);
  or or_88 (or_88_out, not_55_out, not_56_out);
  or or_89 (or_89_out, or_35_out, c);
  or or_90 (or_90_out, or_89_out, or_91_out);
  or or_91 (or_91_out, d, not_57_out);
  or or_92 (or_92_out, or_36_out, c);
  or or_93 (or_93_out, or_92_out, or_94_out);
  or or_94 (or_94_out, not_58_out, e);
  or or_95 (or_95_out, or_37_out, not_59_out);
  or or_96 (or_96_out, or_95_out, or_97_out);
  or or_97 (or_97_out, d, e);
  or or_98 (or_98_out, or_38_out, not_60_out);
  or or_99 (or_99_out, or_98_out, or_100_out);
  or or_100 (or_100_out, not_61_out, not_62_out);
  or or_101 (or_101_out, or_39_out, c);
  or or_102 (or_102_out, or_101_out, or_103_out);
  or or_103 (or_103_out, d, e);
  or or_104 (or_104_out, or_40_out, c);
  or or_105 (or_105_out, or_104_out, or_106_out);
  or or_106 (or_106_out, not_63_out, not_64_out);
  or or_107 (or_107_out, or_41_out, not_65_out);
  or or_108 (or_108_out, or_107_out, or_109_out);
  or or_109 (or_109_out, d, not_66_out);
  or or_110 (or_110_out, or_42_out, not_67_out);
  or or_111 (or_111_out, or_110_out, or_112_out);
  or or_112 (or_112_out, not_68_out, e);
  or or_113 (or_113_out, or_43_out, or_44_out);
  or or_114 (o1, or_113_out, or_115_out);
  or or_115 (or_115_out, or_45_out, or_46_out);
  and and_17 (and_17_out, and_11_out, and_12_out);
  and and_18 (and_18_out, and_13_out, or_54_out);
  and and_19 (and_19_out, and_14_out, and_15_out);
  and and_20 (and_20_out, and_16_out, or_63_out);
  and and_21 (and_21_out, or_66_out, or_69_out);
  and and_22 (and_22_out, or_72_out, or_75_out);
  and and_23 (and_23_out, or_78_out, or_81_out);
  and and_24 (and_24_out, or_84_out, or_87_out);
  and and_25 (and_25_out, or_90_out, or_93_out);
  and and_26 (and_26_out, or_96_out, or_99_out);
  and and_27 (and_27_out, or_102_out, or_105_out);
  and and_28 (and_28_out, or_108_out, or_111_out);
  and and_29 (and_29_out, and_17_out, and_18_out);
  and and_30 (and_30_out, and_19_out, and_20_out);
  and and_31 (and_31_out, and_21_out, and_22_out);
  and and_32 (and_32_out, and_23_out, and_24_out);
  and and_33 (and_33_out, and_25_out, and_26_out);
  and and_34 (and_34_out, and_27_out, and_28_out);
  and and_35 (o2, and_29_out, and_30_out);
  and and_36 (and_36_out, and_31_out, and_32_out);
  and and_37 (and_37_out, and_33_out, and_34_out);
  and and_38 (o3, and_36_out, and_37_out);
endmodule

module _1_2_min_o3_logicfriday (
  input  A,
  input  B,
  input  C,
  input  D,
  input  E,
  output o1,
  output o2,
  output o3
);

  wire and_1_out, and_2_out, and_3_out, and_4_out, and_5_out, and_6_out, and_7_out, and_8_out, and_9_out,
       and_10_out, and_11_out, and_12_out, and_13_out, and_14_out, and_15_out, and_16_out, and_17_out,
       and_18_out, and_19_out, and_20_out, and_21_out, and_22_out, and_23_out, and_24_out, and_25_out,
       and_26_out, and_27_out, and_28_out, and_29_out, and_30_out, and_31_out, and_32_out, and_33_out,
       and_34_out, and_35_out, and_36_out, and_37_out, and_38_out, and_39_out, and_40_out, and_41_out,
       and_42_out, and_43_out, and_44_out, and_45_out, and_46_out, and_47_out, and_48_out, and_49_out,
       and_50_out, and_51_out, and_52_out, and_53_out, and_54_out, and_55_out, and_56_out, and_57_out,
       and_58_out, and_59_out, and_60_out, and_61_out, and_62_out, and_63_out, and_64_out, and_65_out,
       and_66_out, and_67_out, and_68_out, and_69_out, and_70_out, and_71_out, and_72_out, and_73_out,
       and_74_out, and_75_out, and_76_out, and_77_out, and_78_out, and_79_out, and_80_out, and_81_out,
       and_82_out, and_83_out, and_84_out, and_85_out, and_86_out, not_1_out, not_2_out, not_3_out,
       not_4_out, not_5_out, not_6_out, not_7_out, not_8_out, not_9_out, not_10_out, not_11_out, not_12_out,
       not_13_out, not_14_out, not_15_out, not_16_out, not_17_out, not_18_out, not_19_out, not_20_out,
       not_21_out, not_22_out, not_23_out, not_24_out, not_25_out, not_26_out, not_27_out, not_28_out,
       not_29_out, not_30_out, not_31_out, not_32_out, not_33_out, not_34_out, not_35_out, not_36_out,
       not_37_out, not_38_out, not_39_out, not_40_out, not_41_out, not_42_out, not_43_out, not_44_out,
       not_45_out, not_46_out, not_47_out, not_48_out, not_49_out, not_50_out, not_51_out, not_52_out,
       not_53_out, not_54_out, not_55_out, not_56_out, not_57_out, not_58_out, not_59_out, not_60_out,
       not_61_out, not_62_out, not_63_out, not_64_out, not_65_out, not_66_out, not_67_out, not_68_out,
       or_1_out, or_2_out, or_3_out, or_4_out, or_5_out, or_6_out, or_7_out, or_8_out, or_9_out, or_10_out,
       or_11_out, or_12_out, or_13_out, or_14_out, or_15_out, or_16_out, or_17_out, or_18_out, or_19_out,
       or_20_out, or_21_out, or_22_out, or_23_out, or_24_out, or_25_out, or_26_out, or_27_out, or_28_out,
       or_29_out, or_30_out, or_31_out, or_32_out, or_33_out, or_34_out, or_35_out, or_36_out, or_37_out,
       or_38_out, or_39_out, or_40_out, or_41_out, or_42_out, or_43_out, or_44_out, or_45_out, or_46_out,
       or_47_out, or_48_out, or_49_out, or_51_out, or_52_out, or_53_out, or_54_out, or_55_out, or_56_out,
       or_57_out, or_58_out, or_59_out, or_60_out, or_61_out, or_62_out, or_63_out, or_64_out, or_65_out;

  and and_1 (and_1_out, D, E);
  and and_2 (and_2_out, C, E);
  and and_3 (and_3_out, B, C);
  and and_4 (and_4_out, A, E);
  not not_1 (not_1_out, D);
  not not_2 (not_2_out, E);
  not not_3 (not_3_out, C);
  not not_4 (not_4_out, E);
  not not_5 (not_5_out, C);
  not not_6 (not_6_out, D);
  not not_7 (not_7_out, B);
  not not_8 (not_8_out, E);
  not not_9 (not_9_out, B);
  not not_10 (not_10_out, D);
  not not_11 (not_11_out, B);
  not not_12 (not_12_out, C);
  not not_13 (not_13_out, A);
  not not_14 (not_14_out, E);
  not not_15 (not_15_out, A);
  not not_16 (not_16_out, D);
  not not_17 (not_17_out, A);
  not not_18 (not_18_out, C);
  not not_19 (not_19_out, A);
  not not_20 (not_20_out, C);
  not not_21 (not_21_out, A);
  not not_22 (not_22_out, B);
  not not_23 (not_23_out, A);
  not not_24 (not_24_out, B);
  not not_25 (not_25_out, B);
  not not_26 (not_26_out, A);
  not not_27 (not_27_out, A);
  not not_28 (not_28_out, B);
  not not_29 (not_29_out, A);
  not not_30 (not_30_out, B);
  not not_31 (not_31_out, A);
  not not_32 (not_32_out, B);
  not not_33 (not_33_out, A);
  not not_34 (not_34_out, A);
  not not_35 (not_35_out, A);
  not not_36 (not_36_out, A);
  not not_37 (not_37_out, B);
  not not_38 (not_38_out, B);
  not not_39 (not_39_out, B);
  not not_40 (not_40_out, B);
  or or_1 (or_1_out, and_1_out, and_2_out);
  and and_5 (and_5_out, C, D);
  and and_6 (and_6_out, B, E);
  and and_7 (and_7_out, B, D);
  or or_2 (or_2_out, and_3_out, and_4_out);
  and and_8 (and_8_out, A, D);
  and and_9 (and_9_out, A, C);
  and and_10 (and_10_out, A, B);
  or or_3 (or_3_out, A, B);
  or or_4 (or_4_out, not_1_out, not_2_out);
  or or_5 (or_5_out, A, B);
  or or_6 (or_6_out, not_3_out, not_4_out);
  or or_7 (or_7_out, A, B);
  or or_8 (or_8_out, not_5_out, not_6_out);
  or or_9 (or_9_out, A, not_7_out);
  or or_10 (or_10_out, C, not_8_out);
  or or_11 (or_11_out, A, not_9_out);
  or or_12 (or_12_out, C, not_10_out);
  or or_13 (or_13_out, A, not_11_out);
  or or_14 (or_14_out, not_12_out, D);
  not not_41 (not_41_out, B);
  not not_42 (not_42_out, C);
  or or_15 (or_15_out, not_13_out, B);
  or or_16 (or_16_out, C, not_14_out);
  or or_17 (or_17_out, not_15_out, B);
  or or_18 (or_18_out, C, not_16_out);
  or or_19 (or_19_out, not_17_out, B);
  or or_20 (or_20_out, not_18_out, D);
  or or_21 (or_21_out, not_19_out, B);
  or or_22 (or_22_out, not_20_out, E);
  or or_23 (or_23_out, not_21_out, not_22_out);
  or or_24 (or_24_out, C, D);
  or or_25 (or_25_out, not_23_out, not_24_out);
  or or_26 (or_26_out, C, E);
  not not_43 (not_43_out, A);
  not not_44 (not_44_out, B);
  and and_11 (and_11_out, A, not_25_out);
  not not_45 (not_45_out, C);
  not not_46 (not_46_out, D);
  not not_47 (not_47_out, E);
  and and_12 (and_12_out, not_26_out, B);
  not not_48 (not_48_out, C);
  not not_49 (not_49_out, D);
  not not_50 (not_50_out, E);
  and and_13 (and_13_out, not_27_out, not_28_out);
  not not_51 (not_51_out, D);
  not not_52 (not_52_out, E);
  and and_14 (and_14_out, not_29_out, not_30_out);
  not not_53 (not_53_out, C);
  not not_54 (not_54_out, E);
  and and_15 (and_15_out, not_31_out, not_32_out);
  not not_55 (not_55_out, C);
  not not_56 (not_56_out, D);
  and and_16 (and_16_out, not_33_out, B);
  not not_57 (not_57_out, E);
  and and_17 (and_17_out, not_34_out, B);
  not not_58 (not_58_out, D);
  and and_18 (and_18_out, not_35_out, B);
  not not_59 (not_59_out, C);
  and and_19 (and_19_out, not_36_out, not_37_out);
  and and_20 (and_20_out, A, B);
  not not_60 (not_60_out, D);
  not not_61 (not_61_out, E);
  and and_21 (and_21_out, A, B);
  not not_62 (not_62_out, C);
  not not_63 (not_63_out, E);
  and and_22 (and_22_out, A, not_38_out);
  not not_64 (not_64_out, E);
  and and_23 (and_23_out, A, B);
  not not_65 (not_65_out, C);
  not not_66 (not_66_out, D);
  and and_24 (and_24_out, A, not_39_out);
  not not_67 (not_67_out, D);
  and and_25 (and_25_out, A, not_40_out);
  not not_68 (not_68_out, C);
  and and_26 (and_26_out, A, B);
  or or_27 (or_27_out, or_1_out, and_5_out);
  or or_28 (or_28_out, and_6_out, and_7_out);
  or or_29 (or_29_out, or_2_out, and_8_out);
  or or_30 (or_30_out, and_9_out, and_10_out);
  or or_31 (or_31_out, or_3_out, or_4_out);
  and and_27 (and_27_out, or_31_out, or_32_out);
  or or_32 (or_32_out, or_5_out, or_6_out);
  or or_33 (or_33_out, or_7_out, or_8_out);
  and and_28 (and_28_out, or_33_out, or_34_out);
  or or_34 (or_34_out, or_9_out, or_10_out);
  or or_35 (or_35_out, or_11_out, or_12_out);
  and and_29 (and_29_out, or_35_out, or_36_out);
  or or_36 (or_36_out, or_13_out, or_14_out);
  or or_37 (or_37_out, A, not_41_out);
  or or_38 (or_38_out, or_37_out, or_39_out);
  or or_39 (or_39_out, not_42_out, E);
  or or_40 (or_40_out, or_15_out, or_16_out);
  and and_30 (and_30_out, or_40_out, or_41_out);
  or or_41 (or_41_out, or_17_out, or_18_out);
  or or_42 (or_42_out, or_19_out, or_20_out);
  and and_31 (and_31_out, or_42_out, or_43_out);
  or or_43 (or_43_out, or_21_out, or_22_out);
  or or_44 (or_44_out, or_23_out, or_24_out);
  and and_32 (and_32_out, or_44_out, or_45_out);
  or or_45 (or_45_out, or_25_out, or_26_out);
  or or_46 (or_46_out, not_43_out, not_44_out);
  or or_47 (or_47_out, or_46_out, or_48_out);
  or or_48 (or_48_out, D, E);
  and and_33 (and_33_out, and_11_out, not_45_out);
  and and_34 (and_34_out, and_33_out, and_35_out);
  and and_35 (and_35_out, not_46_out, not_47_out);
  and and_36 (and_36_out, and_12_out, not_48_out);
  and and_37 (and_37_out, and_36_out, and_38_out);
  and and_38 (and_38_out, not_49_out, not_50_out);
  and and_39 (and_39_out, and_13_out, C);
  and and_40 (and_40_out, and_39_out, and_41_out);
  and and_41 (and_41_out, not_51_out, not_52_out);
  and and_42 (and_42_out, and_14_out, not_53_out);
  and and_43 (and_43_out, and_42_out, and_44_out);
  and and_44 (and_44_out, D, not_54_out);
  and and_45 (and_45_out, and_15_out, not_55_out);
  and and_46 (and_46_out, and_45_out, and_47_out);
  and and_47 (and_47_out, not_56_out, E);
  and and_48 (and_48_out, and_16_out, C);
  and and_49 (and_49_out, and_48_out, and_50_out);
  and and_50 (and_50_out, D, not_57_out);
  and and_51 (and_51_out, and_17_out, C);
  and and_52 (and_52_out, and_51_out, and_53_out);
  and and_53 (and_53_out, not_58_out, E);
  and and_54 (and_54_out, and_18_out, not_59_out);
  and and_55 (and_55_out, and_54_out, and_56_out);
  and and_56 (and_56_out, D, E);
  and and_57 (and_57_out, and_19_out, C);
  and and_58 (and_58_out, and_57_out, and_59_out);
  and and_59 (and_59_out, D, E);
  and and_60 (and_60_out, and_20_out, C);
  and and_61 (and_61_out, and_60_out, and_62_out);
  and and_62 (and_62_out, not_60_out, not_61_out);
  and and_63 (and_63_out, and_21_out, not_62_out);
  and and_64 (and_64_out, and_63_out, and_65_out);
  and and_65 (and_65_out, D, not_63_out);
  and and_66 (and_66_out, and_22_out, C);
  and and_67 (and_67_out, and_66_out, and_68_out);
  and and_68 (and_68_out, D, not_64_out);
  and and_69 (and_69_out, and_23_out, not_65_out);
  and and_70 (and_70_out, and_69_out, and_71_out);
  and and_71 (and_71_out, not_66_out, E);
  and and_72 (and_72_out, and_24_out, C);
  and and_73 (and_73_out, and_72_out, and_74_out);
  and and_74 (and_74_out, not_67_out, E);
  and and_75 (and_75_out, and_25_out, not_68_out);
  and and_76 (and_76_out, and_75_out, and_77_out);
  and and_77 (and_77_out, D, E);
  and and_78 (and_78_out, and_26_out, C);
  and and_79 (and_79_out, and_78_out, and_80_out);
  and and_80 (and_80_out, D, E);
  or or_49 (or_49_out, or_27_out, or_28_out);
  or or_50 (o1, or_49_out, or_51_out);
  or or_51 (or_51_out, or_29_out, or_30_out);
  and and_81 (and_81_out, and_27_out, and_28_out);
  and and_82 (and_82_out, and_29_out, or_38_out);
  and and_83 (and_83_out, and_30_out, and_31_out);
  and and_84 (and_84_out, and_32_out, or_47_out);
  or or_52 (or_52_out, and_34_out, and_37_out);
  or or_53 (or_53_out, and_40_out, and_43_out);
  or or_54 (or_54_out, and_46_out, and_49_out);
  or or_55 (or_55_out, and_52_out, and_55_out);
  or or_56 (or_56_out, and_58_out, and_61_out);
  or or_57 (or_57_out, and_64_out, and_67_out);
  or or_58 (or_58_out, and_70_out, and_73_out);
  or or_59 (or_59_out, and_76_out, and_79_out);
  and and_85 (and_85_out, and_81_out, and_82_out);
  and and_86 (and_86_out, and_83_out, and_84_out);
  or or_60 (or_60_out, or_52_out, or_53_out);
  or or_61 (or_61_out, or_54_out, or_55_out);
  or or_62 (or_62_out, or_56_out, or_57_out);
  or or_63 (or_63_out, or_58_out, or_59_out);
  and and_87 (o2, and_85_out, and_86_out);
  or or_64 (or_64_out, or_60_out, or_61_out);
  or or_65 (or_65_out, or_62_out, or_63_out);
  or or_66 (o3, or_64_out, or_65_out);
endmodule

module _1_2_min_o1_logicfriday (
  input  A,
  input  B,
  input  C,
  input  D,
  input  E,
  output o1,
  output o2,
  output o3
);

  wire and_1_out, and_2_out, and_3_out, and_4_out, and_5_out, and_6_out, and_7_out, and_8_out, and_9_out,
       and_10_out, and_11_out, and_12_out, and_13_out, and_14_out, and_15_out, and_16_out, and_17_out,
       and_18_out, and_19_out, and_20_out, and_21_out, and_22_out, and_23_out, and_24_out, and_25_out,
       and_26_out, and_27_out, and_28_out, and_29_out, and_30_out, and_31_out, and_32_out, and_33_out,
       and_34_out, and_35_out, and_36_out, and_37_out, and_38_out, and_39_out, and_40_out, and_41_out,
       and_42_out, and_43_out, and_44_out, and_45_out, and_46_out, and_47_out, and_48_out, and_49_out,
       and_50_out, and_51_out, and_52_out, and_53_out, and_54_out, and_55_out, and_56_out, and_57_out,
       and_58_out, and_59_out, and_60_out, and_61_out, and_62_out, and_63_out, and_64_out, and_65_out,
       and_66_out, and_67_out, and_68_out, and_69_out, and_70_out, and_71_out, and_72_out, and_73_out,
       and_74_out, and_75_out, and_76_out, and_77_out, and_78_out, and_79_out, and_80_out, and_81_out,
       and_82_out, and_83_out, and_84_out, and_85_out, and_86_out, not_1_out, not_2_out, not_3_out,
       not_4_out, not_5_out, not_6_out, not_7_out, not_8_out, not_9_out, not_10_out, not_11_out, not_12_out,
       not_13_out, not_14_out, not_15_out, not_16_out, not_17_out, not_18_out, not_19_out, not_20_out,
       not_21_out, not_22_out, not_23_out, not_24_out, not_25_out, not_26_out, not_27_out, not_28_out,
       not_29_out, not_30_out, not_31_out, not_32_out, not_33_out, not_34_out, not_35_out, not_36_out,
       not_37_out, not_38_out, not_39_out, not_40_out, not_41_out, not_42_out, not_43_out, not_44_out,
       not_45_out, not_46_out, not_47_out, not_48_out, not_49_out, not_50_out, not_51_out, not_52_out,
       not_53_out, not_54_out, not_55_out, not_56_out, not_57_out, not_58_out, not_59_out, not_60_out,
       not_61_out, not_62_out, not_63_out, not_64_out, not_65_out, not_66_out, not_67_out, not_68_out,
       or_1_out, or_2_out, or_3_out, or_4_out, or_5_out, or_6_out, or_7_out, or_8_out, or_9_out, or_10_out,
       or_11_out, or_12_out, or_13_out, or_14_out, or_15_out, or_16_out, or_17_out, or_18_out, or_19_out,
       or_20_out, or_21_out, or_22_out, or_23_out, or_24_out, or_25_out, or_26_out, or_27_out, or_28_out,
       or_29_out, or_30_out, or_31_out, or_32_out, or_33_out, or_34_out, or_35_out, or_36_out, or_37_out,
       or_38_out, or_39_out, or_40_out, or_41_out, or_42_out, or_43_out, or_44_out, or_45_out, or_46_out,
       or_47_out, or_48_out, or_49_out, or_51_out, or_52_out, or_53_out, or_54_out, or_55_out, or_56_out,
       or_57_out, or_58_out, or_59_out, or_60_out, or_61_out, or_62_out, or_63_out, or_64_out, or_65_out;

  and and_1 (and_1_out, A, B);
  and and_2 (and_2_out, A, C);
  and and_3 (and_3_out, C, D);
  and and_4 (and_4_out, A, E);
  not not_1 (not_1_out, D);
  not not_2 (not_2_out, E);
  not not_3 (not_3_out, C);
  not not_4 (not_4_out, E);
  not not_5 (not_5_out, C);
  not not_6 (not_6_out, D);
  not not_7 (not_7_out, B);
  not not_8 (not_8_out, E);
  not not_9 (not_9_out, B);
  not not_10 (not_10_out, D);
  not not_11 (not_11_out, B);
  not not_12 (not_12_out, C);
  not not_13 (not_13_out, A);
  not not_14 (not_14_out, E);
  not not_15 (not_15_out, A);
  not not_16 (not_16_out, D);
  not not_17 (not_17_out, A);
  not not_18 (not_18_out, C);
  not not_19 (not_19_out, A);
  not not_20 (not_20_out, C);
  not not_21 (not_21_out, A);
  not not_22 (not_22_out, B);
  not not_23 (not_23_out, A);
  not not_24 (not_24_out, B);
  not not_25 (not_25_out, B);
  not not_26 (not_26_out, A);
  not not_27 (not_27_out, A);
  not not_28 (not_28_out, B);
  not not_29 (not_29_out, A);
  not not_30 (not_30_out, B);
  not not_31 (not_31_out, A);
  not not_32 (not_32_out, B);
  not not_33 (not_33_out, A);
  not not_34 (not_34_out, A);
  not not_35 (not_35_out, A);
  not not_36 (not_36_out, A);
  not not_37 (not_37_out, B);
  not not_38 (not_38_out, B);
  not not_39 (not_39_out, B);
  not not_40 (not_40_out, B);
  or or_1 (or_1_out, and_1_out, and_2_out);
  and and_5 (and_5_out, B, C);
  and and_6 (and_6_out, A, D);
  and and_7 (and_7_out, B, D);
  or or_2 (or_2_out, and_3_out, and_4_out);
  and and_8 (and_8_out, B, E);
  and and_9 (and_9_out, C, E);
  and and_10 (and_10_out, D, E);
  or or_3 (or_3_out, A, B);
  or or_4 (or_4_out, not_1_out, not_2_out);
  or or_5 (or_5_out, A, B);
  or or_6 (or_6_out, not_3_out, not_4_out);
  or or_7 (or_7_out, A, B);
  or or_8 (or_8_out, not_5_out, not_6_out);
  or or_9 (or_9_out, A, not_7_out);
  or or_10 (or_10_out, C, not_8_out);
  or or_11 (or_11_out, A, not_9_out);
  or or_12 (or_12_out, C, not_10_out);
  or or_13 (or_13_out, A, not_11_out);
  or or_14 (or_14_out, not_12_out, D);
  not not_41 (not_41_out, B);
  not not_42 (not_42_out, C);
  or or_15 (or_15_out, not_13_out, B);
  or or_16 (or_16_out, C, not_14_out);
  or or_17 (or_17_out, not_15_out, B);
  or or_18 (or_18_out, C, not_16_out);
  or or_19 (or_19_out, not_17_out, B);
  or or_20 (or_20_out, not_18_out, D);
  or or_21 (or_21_out, not_19_out, B);
  or or_22 (or_22_out, not_20_out, E);
  or or_23 (or_23_out, not_21_out, not_22_out);
  or or_24 (or_24_out, C, D);
  or or_25 (or_25_out, not_23_out, not_24_out);
  or or_26 (or_26_out, C, E);
  not not_43 (not_43_out, A);
  not not_44 (not_44_out, B);
  and and_11 (and_11_out, A, not_25_out);
  not not_45 (not_45_out, C);
  not not_46 (not_46_out, D);
  not not_47 (not_47_out, E);
  and and_12 (and_12_out, not_26_out, B);
  not not_48 (not_48_out, C);
  not not_49 (not_49_out, D);
  not not_50 (not_50_out, E);
  and and_13 (and_13_out, not_27_out, not_28_out);
  not not_51 (not_51_out, D);
  not not_52 (not_52_out, E);
  and and_14 (and_14_out, not_29_out, not_30_out);
  not not_53 (not_53_out, C);
  not not_54 (not_54_out, E);
  and and_15 (and_15_out, not_31_out, not_32_out);
  not not_55 (not_55_out, C);
  not not_56 (not_56_out, D);
  and and_16 (and_16_out, not_33_out, B);
  not not_57 (not_57_out, E);
  and and_17 (and_17_out, not_34_out, B);
  not not_58 (not_58_out, D);
  and and_18 (and_18_out, not_35_out, B);
  not not_59 (not_59_out, C);
  and and_19 (and_19_out, not_36_out, not_37_out);
  and and_20 (and_20_out, A, B);
  not not_60 (not_60_out, D);
  not not_61 (not_61_out, E);
  and and_21 (and_21_out, A, B);
  not not_62 (not_62_out, C);
  not not_63 (not_63_out, E);
  and and_22 (and_22_out, A, not_38_out);
  not not_64 (not_64_out, E);
  and and_23 (and_23_out, A, B);
  not not_65 (not_65_out, C);
  not not_66 (not_66_out, D);
  and and_24 (and_24_out, A, not_39_out);
  not not_67 (not_67_out, D);
  and and_25 (and_25_out, A, not_40_out);
  not not_68 (not_68_out, C);
  and and_26 (and_26_out, A, B);
  or or_27 (or_27_out, or_1_out, and_5_out);
  or or_28 (or_28_out, and_6_out, and_7_out);
  or or_29 (or_29_out, or_2_out, and_8_out);
  or or_30 (or_30_out, and_9_out, and_10_out);
  or or_31 (or_31_out, or_3_out, or_4_out);
  and and_27 (and_27_out, or_31_out, or_32_out);
  or or_32 (or_32_out, or_5_out, or_6_out);
  or or_33 (or_33_out, or_7_out, or_8_out);
  and and_28 (and_28_out, or_33_out, or_34_out);
  or or_34 (or_34_out, or_9_out, or_10_out);
  or or_35 (or_35_out, or_11_out, or_12_out);
  and and_29 (and_29_out, or_35_out, or_36_out);
  or or_36 (or_36_out, or_13_out, or_14_out);
  or or_37 (or_37_out, A, not_41_out);
  or or_38 (or_38_out, or_37_out, or_39_out);
  or or_39 (or_39_out, not_42_out, E);
  or or_40 (or_40_out, or_15_out, or_16_out);
  and and_30 (and_30_out, or_40_out, or_41_out);
  or or_41 (or_41_out, or_17_out, or_18_out);
  or or_42 (or_42_out, or_19_out, or_20_out);
  and and_31 (and_31_out, or_42_out, or_43_out);
  or or_43 (or_43_out, or_21_out, or_22_out);
  or or_44 (or_44_out, or_23_out, or_24_out);
  and and_32 (and_32_out, or_44_out, or_45_out);
  or or_45 (or_45_out, or_25_out, or_26_out);
  or or_46 (or_46_out, not_43_out, not_44_out);
  or or_47 (or_47_out, or_46_out, or_48_out);
  or or_48 (or_48_out, D, E);
  and and_33 (and_33_out, and_11_out, not_45_out);
  and and_34 (and_34_out, and_33_out, and_35_out);
  and and_35 (and_35_out, not_46_out, not_47_out);
  and and_36 (and_36_out, and_12_out, not_48_out);
  and and_37 (and_37_out, and_36_out, and_38_out);
  and and_38 (and_38_out, not_49_out, not_50_out);
  and and_39 (and_39_out, and_13_out, C);
  and and_40 (and_40_out, and_39_out, and_41_out);
  and and_41 (and_41_out, not_51_out, not_52_out);
  and and_42 (and_42_out, and_14_out, not_53_out);
  and and_43 (and_43_out, and_42_out, and_44_out);
  and and_44 (and_44_out, D, not_54_out);
  and and_45 (and_45_out, and_15_out, not_55_out);
  and and_46 (and_46_out, and_45_out, and_47_out);
  and and_47 (and_47_out, not_56_out, E);
  and and_48 (and_48_out, and_16_out, C);
  and and_49 (and_49_out, and_48_out, and_50_out);
  and and_50 (and_50_out, D, not_57_out);
  and and_51 (and_51_out, and_17_out, C);
  and and_52 (and_52_out, and_51_out, and_53_out);
  and and_53 (and_53_out, not_58_out, E);
  and and_54 (and_54_out, and_18_out, not_59_out);
  and and_55 (and_55_out, and_54_out, and_56_out);
  and and_56 (and_56_out, D, E);
  and and_57 (and_57_out, and_19_out, C);
  and and_58 (and_58_out, and_57_out, and_59_out);
  and and_59 (and_59_out, D, E);
  and and_60 (and_60_out, and_20_out, C);
  and and_61 (and_61_out, and_60_out, and_62_out);
  and and_62 (and_62_out, not_60_out, not_61_out);
  and and_63 (and_63_out, and_21_out, not_62_out);
  and and_64 (and_64_out, and_63_out, and_65_out);
  and and_65 (and_65_out, D, not_63_out);
  and and_66 (and_66_out, and_22_out, C);
  and and_67 (and_67_out, and_66_out, and_68_out);
  and and_68 (and_68_out, D, not_64_out);
  and and_69 (and_69_out, and_23_out, not_65_out);
  and and_70 (and_70_out, and_69_out, and_71_out);
  and and_71 (and_71_out, not_66_out, E);
  and and_72 (and_72_out, and_24_out, C);
  and and_73 (and_73_out, and_72_out, and_74_out);
  and and_74 (and_74_out, not_67_out, E);
  and and_75 (and_75_out, and_25_out, not_68_out);
  and and_76 (and_76_out, and_75_out, and_77_out);
  and and_77 (and_77_out, D, E);
  and and_78 (and_78_out, and_26_out, C);
  and and_79 (and_79_out, and_78_out, and_80_out);
  and and_80 (and_80_out, D, E);
  or or_49 (or_49_out, or_27_out, or_28_out);
  or or_50 (o1, or_49_out, or_51_out);
  or or_51 (or_51_out, or_29_out, or_30_out);
  and and_81 (and_81_out, and_27_out, and_28_out);
  and and_82 (and_82_out, and_29_out, or_38_out);
  and and_83 (and_83_out, and_30_out, and_31_out);
  and and_84 (and_84_out, and_32_out, or_47_out);
  or or_52 (or_52_out, and_34_out, and_37_out);
  or or_53 (or_53_out, and_40_out, and_43_out);
  or or_54 (or_54_out, and_46_out, and_49_out);
  or or_55 (or_55_out, and_52_out, and_55_out);
  or or_56 (or_56_out, and_58_out, and_61_out);
  or or_57 (or_57_out, and_64_out, and_67_out);
  or or_58 (or_58_out, and_70_out, and_73_out);
  or or_59 (or_59_out, and_76_out, and_79_out);
  and and_85 (and_85_out, and_81_out, and_82_out);
  and and_86 (and_86_out, and_83_out, and_84_out);
  or or_60 (or_60_out, or_52_out, or_53_out);
  or or_61 (or_61_out, or_54_out, or_55_out);
  or or_62 (or_62_out, or_56_out, or_57_out);
  or or_63 (or_63_out, or_58_out, or_59_out);
  and and_87 (o2, and_85_out, and_86_out);
  or or_64 (or_64_out, or_60_out, or_61_out);
  or or_65 (or_65_out, or_62_out, or_63_out);
  or or_66 (o3, or_64_out, or_65_out);
endmodule

module _1_2_min_o2_logicfriday (
  input  A,
  input  B,
  input  C,
  input  D,
  input  E,
  output o1,
  output o2,
  output o3
);

  wire and_1_out, and_2_out, and_3_out, and_4_out, and_5_out, and_6_out, and_7_out, and_8_out, and_9_out,
       and_10_out, and_11_out, and_12_out, and_13_out, and_14_out, and_15_out, and_16_out, and_17_out,
       and_18_out, and_19_out, and_20_out, and_21_out, and_22_out, and_23_out, and_24_out, and_25_out,
       and_26_out, and_27_out, and_28_out, and_29_out, and_30_out, and_31_out, and_32_out, and_33_out,
       and_34_out, and_35_out, and_36_out, and_37_out, and_38_out, and_39_out, and_40_out, and_41_out,
       and_42_out, and_43_out, and_44_out, and_45_out, and_46_out, and_47_out, and_48_out, and_49_out,
       and_50_out, and_51_out, and_52_out, and_53_out, and_54_out, and_55_out, and_56_out, and_57_out,
       and_58_out, and_59_out, and_60_out, and_61_out, and_62_out, and_63_out, and_64_out, and_65_out,
       and_66_out, and_67_out, and_68_out, and_69_out, and_70_out, and_71_out, and_72_out, and_73_out,
       and_74_out, and_75_out, and_76_out, and_77_out, and_78_out, and_79_out, and_80_out, and_81_out,
       and_82_out, and_83_out, and_84_out, and_85_out, and_86_out, and_87_out, and_88_out, and_89_out,
       and_90_out, and_91_out, and_92_out, and_93_out, and_94_out, and_95_out, and_96_out, and_97_out,
       and_98_out, and_99_out, and_100_out, and_101_out, and_102_out, and_103_out, and_104_out, not_1_out,
       not_2_out, not_3_out, not_4_out, not_5_out, not_6_out, not_7_out, not_8_out, not_9_out, not_10_out,
       not_11_out, not_12_out, not_13_out, not_14_out, not_15_out, not_16_out, not_17_out, not_18_out,
       not_19_out, not_20_out, not_21_out, not_22_out, not_23_out, not_24_out, not_25_out, not_26_out,
       not_27_out, not_28_out, not_29_out, not_30_out, not_31_out, not_32_out, not_33_out, not_34_out,
       not_35_out, not_36_out, not_37_out, not_38_out, not_39_out, not_40_out, not_41_out, not_42_out,
       not_43_out, not_44_out, not_45_out, not_46_out, not_47_out, not_48_out, not_49_out, not_50_out,
       not_51_out, not_52_out, not_53_out, not_54_out, not_55_out, not_56_out, not_57_out, not_58_out,
       not_59_out, not_60_out, or_1_out, or_2_out, or_3_out, or_4_out, or_5_out, or_6_out, or_7_out,
       or_8_out, or_9_out, or_11_out, or_12_out, or_13_out, or_14_out, or_15_out, or_16_out, or_17_out,
       or_18_out, or_19_out, or_20_out, or_21_out, or_22_out, or_23_out, or_24_out, or_25_out, or_26_out,
       or_27_out, or_28_out, or_29_out, or_31_out, or_32_out;

  and and_1 (and_1_out, A, B);
  and and_2 (and_2_out, A, C);
  and and_3 (and_3_out, C, D);
  and and_4 (and_4_out, A, E);
  not not_1 (not_1_out, A);
  not not_2 (not_2_out, B);
  not not_3 (not_3_out, C);
  not not_4 (not_4_out, D);
  not not_5 (not_5_out, A);
  not not_6 (not_6_out, B);
  not not_7 (not_7_out, C);
  not not_8 (not_8_out, E);
  not not_9 (not_9_out, B);
  not not_10 (not_10_out, A);
  not not_11 (not_11_out, A);
  not not_12 (not_12_out, B);
  not not_13 (not_13_out, A);
  not not_14 (not_14_out, B);
  not not_15 (not_15_out, A);
  not not_16 (not_16_out, B);
  not not_17 (not_17_out, A);
  not not_18 (not_18_out, A);
  not not_19 (not_19_out, A);
  not not_20 (not_20_out, A);
  not not_21 (not_21_out, B);
  not not_22 (not_22_out, B);
  not not_23 (not_23_out, B);
  not not_24 (not_24_out, B);
  or or_1 (or_1_out, and_1_out, and_2_out);
  and and_5 (and_5_out, B, C);
  and and_6 (and_6_out, A, D);
  and and_7 (and_7_out, B, D);
  or or_2 (or_2_out, and_3_out, and_4_out);
  and and_8 (and_8_out, B, E);
  and and_9 (and_9_out, C, E);
  and and_10 (and_10_out, D, E);
  and and_11 (and_11_out, A, B);
  and and_12 (and_12_out, C, D);
  and and_13 (and_13_out, not_1_out, not_2_out);
  and and_14 (and_14_out, not_3_out, not_4_out);
  and and_15 (and_15_out, B, C);
  and and_16 (and_16_out, D, E);
  and and_17 (and_17_out, not_5_out, not_6_out);
  and and_18 (and_18_out, not_7_out, not_8_out);
  not not_25 (not_25_out, A);
  not not_26 (not_26_out, B);
  not not_27 (not_27_out, D);
  not not_28 (not_28_out, E);
  not not_29 (not_29_out, A);
  not not_30 (not_30_out, C);
  not not_31 (not_31_out, D);
  not not_32 (not_32_out, E);
  not not_33 (not_33_out, B);
  not not_34 (not_34_out, C);
  not not_35 (not_35_out, D);
  not not_36 (not_36_out, E);
  and and_19 (and_19_out, A, not_9_out);
  not not_37 (not_37_out, C);
  not not_38 (not_38_out, D);
  not not_39 (not_39_out, E);
  and and_20 (and_20_out, not_10_out, B);
  not not_40 (not_40_out, C);
  not not_41 (not_41_out, D);
  not not_42 (not_42_out, E);
  and and_21 (and_21_out, not_11_out, not_12_out);
  not not_43 (not_43_out, D);
  not not_44 (not_44_out, E);
  and and_22 (and_22_out, not_13_out, not_14_out);
  not not_45 (not_45_out, C);
  not not_46 (not_46_out, E);
  and and_23 (and_23_out, not_15_out, not_16_out);
  not not_47 (not_47_out, C);
  not not_48 (not_48_out, D);
  and and_24 (and_24_out, not_17_out, B);
  not not_49 (not_49_out, E);
  and and_25 (and_25_out, not_18_out, B);
  not not_50 (not_50_out, D);
  and and_26 (and_26_out, not_19_out, B);
  not not_51 (not_51_out, C);
  and and_27 (and_27_out, not_20_out, not_21_out);
  and and_28 (and_28_out, A, B);
  not not_52 (not_52_out, D);
  not not_53 (not_53_out, E);
  and and_29 (and_29_out, A, B);
  not not_54 (not_54_out, C);
  not not_55 (not_55_out, E);
  and and_30 (and_30_out, A, not_22_out);
  not not_56 (not_56_out, E);
  and and_31 (and_31_out, A, B);
  not not_57 (not_57_out, C);
  not not_58 (not_58_out, D);
  and and_32 (and_32_out, A, not_23_out);
  not not_59 (not_59_out, D);
  and and_33 (and_33_out, A, not_24_out);
  not not_60 (not_60_out, C);
  and and_34 (and_34_out, A, B);
  or or_3 (or_3_out, or_1_out, and_5_out);
  or or_4 (or_4_out, and_6_out, and_7_out);
  or or_5 (or_5_out, or_2_out, and_8_out);
  or or_6 (or_6_out, and_9_out, and_10_out);
  and and_35 (and_35_out, and_11_out, and_12_out);
  or or_7 (or_7_out, and_35_out, and_36_out);
  and and_36 (and_36_out, and_13_out, and_14_out);
  and and_37 (and_37_out, A, B);
  and and_38 (and_38_out, and_37_out, and_39_out);
  and and_39 (and_39_out, C, E);
  and and_40 (and_40_out, A, B);
  and and_41 (and_41_out, and_40_out, and_42_out);
  and and_42 (and_42_out, D, E);
  and and_43 (and_43_out, A, C);
  and and_44 (and_44_out, and_43_out, and_45_out);
  and and_45 (and_45_out, D, E);
  and and_46 (and_46_out, and_15_out, and_16_out);
  or or_8 (or_8_out, and_46_out, and_47_out);
  and and_47 (and_47_out, and_17_out, and_18_out);
  and and_48 (and_48_out, not_25_out, not_26_out);
  and and_49 (and_49_out, and_48_out, and_50_out);
  and and_50 (and_50_out, not_27_out, not_28_out);
  and and_51 (and_51_out, not_29_out, not_30_out);
  and and_52 (and_52_out, and_51_out, and_53_out);
  and and_53 (and_53_out, not_31_out, not_32_out);
  and and_54 (and_54_out, not_33_out, not_34_out);
  and and_55 (and_55_out, and_54_out, and_56_out);
  and and_56 (and_56_out, not_35_out, not_36_out);
  and and_57 (and_57_out, and_19_out, not_37_out);
  and and_58 (and_58_out, and_57_out, and_59_out);
  and and_59 (and_59_out, not_38_out, not_39_out);
  and and_60 (and_60_out, and_20_out, not_40_out);
  and and_61 (and_61_out, and_60_out, and_62_out);
  and and_62 (and_62_out, not_41_out, not_42_out);
  and and_63 (and_63_out, and_21_out, C);
  and and_64 (and_64_out, and_63_out, and_65_out);
  and and_65 (and_65_out, not_43_out, not_44_out);
  and and_66 (and_66_out, and_22_out, not_45_out);
  and and_67 (and_67_out, and_66_out, and_68_out);
  and and_68 (and_68_out, D, not_46_out);
  and and_69 (and_69_out, and_23_out, not_47_out);
  and and_70 (and_70_out, and_69_out, and_71_out);
  and and_71 (and_71_out, not_48_out, E);
  and and_72 (and_72_out, and_24_out, C);
  and and_73 (and_73_out, and_72_out, and_74_out);
  and and_74 (and_74_out, D, not_49_out);
  and and_75 (and_75_out, and_25_out, C);
  and and_76 (and_76_out, and_75_out, and_77_out);
  and and_77 (and_77_out, not_50_out, E);
  and and_78 (and_78_out, and_26_out, not_51_out);
  and and_79 (and_79_out, and_78_out, and_80_out);
  and and_80 (and_80_out, D, E);
  and and_81 (and_81_out, and_27_out, C);
  and and_82 (and_82_out, and_81_out, and_83_out);
  and and_83 (and_83_out, D, E);
  and and_84 (and_84_out, and_28_out, C);
  and and_85 (and_85_out, and_84_out, and_86_out);
  and and_86 (and_86_out, not_52_out, not_53_out);
  and and_87 (and_87_out, and_29_out, not_54_out);
  and and_88 (and_88_out, and_87_out, and_89_out);
  and and_89 (and_89_out, D, not_55_out);
  and and_90 (and_90_out, and_30_out, C);
  and and_91 (and_91_out, and_90_out, and_92_out);
  and and_92 (and_92_out, D, not_56_out);
  and and_93 (and_93_out, and_31_out, not_57_out);
  and and_94 (and_94_out, and_93_out, and_95_out);
  and and_95 (and_95_out, not_58_out, E);
  and and_96 (and_96_out, and_32_out, C);
  and and_97 (and_97_out, and_96_out, and_98_out);
  and and_98 (and_98_out, not_59_out, E);
  and and_99 (and_99_out, and_33_out, not_60_out);
  and and_100 (and_100_out, and_99_out, and_101_out);
  and and_101 (and_101_out, D, E);
  and and_102 (and_102_out, and_34_out, C);
  and and_103 (and_103_out, and_102_out, and_104_out);
  and and_104 (and_104_out, D, E);
  or or_9 (or_9_out, or_3_out, or_4_out);
  or or_10 (o1, or_9_out, or_11_out);
  or or_11 (or_11_out, or_5_out, or_6_out);
  or or_12 (or_12_out, or_7_out, and_38_out);
  or or_13 (or_13_out, and_41_out, and_44_out);
  or or_14 (or_14_out, or_8_out, and_49_out);
  or or_15 (or_15_out, and_52_out, and_55_out);
  or or_16 (or_16_out, and_58_out, and_61_out);
  or or_17 (or_17_out, and_64_out, and_67_out);
  or or_18 (or_18_out, and_70_out, and_73_out);
  or or_19 (or_19_out, and_76_out, and_79_out);
  or or_20 (or_20_out, and_82_out, and_85_out);
  or or_21 (or_21_out, and_88_out, and_91_out);
  or or_22 (or_22_out, and_94_out, and_97_out);
  or or_23 (or_23_out, and_100_out, and_103_out);
  or or_24 (or_24_out, or_12_out, or_13_out);
  or or_25 (or_25_out, or_14_out, or_15_out);
  or or_26 (or_26_out, or_16_out, or_17_out);
  or or_27 (or_27_out, or_18_out, or_19_out);
  or or_28 (or_28_out, or_20_out, or_21_out);
  or or_29 (or_29_out, or_22_out, or_23_out);
  or or_30 (o2, or_24_out, or_25_out);
  or or_31 (or_31_out, or_26_out, or_27_out);
  or or_32 (or_32_out, or_28_out, or_29_out);
  or or_33 (o3, or_31_out, or_32_out);
endmodule

module \_2_2_o1_min_задание_2__пункт_1  (
  input  A,
  input  B,
  input  C,
  input  D,
  input  E,
  output o1,
  output o2,
  output o3
);

  wire and_1_out, and_2_out, and_3_out, and_4_out, and_5_out, and_6_out, and_7_out, and_8_out, and_9_out,
       and_10_out, and_11_out, and_12_out, and_13_out, and_14_out, and_15_out, and_16_out, and_17_out,
       and_18_out, and_19_out, and_20_out, and_21_out, and_22_out, and_23_out, and_24_out, and_25_out,
       and_26_out, and_27_out, and_28_out, and_29_out, and_30_out, and_31_out, and_32_out, and_33_out,
       and_34_out, and_35_out, and_36_out, and_37_out, and_38_out, and_39_out, and_40_out, and_41_out,
       and_42_out, and_43_out, and_44_out, and_45_out, and_46_out, and_47_out, and_48_out, and_49_out,
       and_50_out, and_51_out, and_52_out, and_53_out, and_54_out, and_55_out, and_56_out, and_57_out,
       and_58_out, and_59_out, and_60_out, and_61_out, and_62_out, and_63_out, and_64_out, and_65_out,
       and_66_out, and_67_out, and_68_out, and_69_out, and_70_out, and_71_out, and_72_out, and_73_out,
       and_74_out, and_75_out, and_76_out, and_77_out, not_1_out, not_2_out, not_3_out, not_4_out, not_5_out,
       not_6_out, not_7_out, not_8_out, not_9_out, not_10_out, not_11_out, not_12_out, not_13_out,
       not_14_out, not_15_out, not_16_out, not_17_out, not_18_out, not_19_out, not_20_out, not_21_out,
       not_22_out, not_23_out, not_24_out, not_25_out, not_26_out, not_27_out, not_28_out, not_29_out,
       not_30_out, not_31_out, not_32_out, not_33_out, not_34_out, not_35_out, not_36_out, not_37_out,
       not_38_out, not_39_out, not_40_out, not_41_out, not_42_out, not_43_out, not_44_out, not_45_out,
       not_46_out, not_47_out, not_48_out, not_49_out, not_50_out, not_51_out, not_52_out, not_53_out,
       not_54_out, not_55_out, not_56_out, not_57_out, not_58_out, not_59_out, not_60_out, not_61_out,
       not_62_out, not_63_out, not_64_out, not_65_out, not_66_out, not_67_out, not_68_out, or_1_out,
       or_2_out, or_3_out, or_4_out, or_5_out, or_6_out, or_7_out, or_8_out, or_9_out, or_10_out, or_11_out,
       or_12_out, or_13_out, or_14_out, or_15_out, or_16_out, or_17_out, or_18_out, or_19_out, or_20_out,
       or_21_out, or_22_out, or_23_out, or_24_out, or_25_out, or_26_out, or_27_out, or_28_out, or_29_out,
       or_30_out, or_31_out, or_32_out, or_33_out, or_34_out, or_35_out, or_36_out, or_37_out, or_38_out,
       or_39_out, or_40_out, or_41_out, or_42_out, or_43_out, or_44_out, or_45_out, or_46_out, or_47_out,
       or_48_out, or_49_out, or_51_out, or_52_out, or_53_out, or_54_out, or_55_out, or_56_out, or_57_out,
       or_58_out, or_59_out, or_60_out, or_61_out, or_62_out, or_63_out, or_64_out;

  and and_1 (and_1_out, D, E);
  and and_2 (and_2_out, C, E);
  and and_3 (and_3_out, B, C);
  and and_4 (and_4_out, A, E);
  not not_1 (not_1_out, D);
  not not_2 (not_2_out, E);
  not not_3 (not_3_out, C);
  not not_4 (not_4_out, E);
  not not_5 (not_5_out, C);
  not not_6 (not_6_out, D);
  not not_7 (not_7_out, B);
  not not_8 (not_8_out, E);
  not not_9 (not_9_out, B);
  not not_10 (not_10_out, D);
  not not_11 (not_11_out, B);
  not not_12 (not_12_out, C);
  not not_13 (not_13_out, A);
  not not_14 (not_14_out, E);
  not not_15 (not_15_out, A);
  not not_16 (not_16_out, D);
  not not_17 (not_17_out, A);
  not not_18 (not_18_out, C);
  not not_19 (not_19_out, A);
  not not_20 (not_20_out, C);
  not not_21 (not_21_out, A);
  not not_22 (not_22_out, B);
  not not_23 (not_23_out, A);
  not not_24 (not_24_out, B);
  not not_25 (not_25_out, A);
  not not_26 (not_26_out, B);
  not not_27 (not_27_out, A);
  not not_28 (not_28_out, A);
  not not_29 (not_29_out, A);
  not not_30 (not_30_out, B);
  not not_31 (not_31_out, B);
  not not_32 (not_32_out, B);
  or or_1 (or_1_out, and_1_out, and_2_out);
  and and_5 (and_5_out, C, D);
  and and_6 (and_6_out, B, E);
  and and_7 (and_7_out, B, D);
  or or_2 (or_2_out, and_3_out, and_4_out);
  and and_8 (and_8_out, A, D);
  and and_9 (and_9_out, A, C);
  and and_10 (and_10_out, A, B);
  or or_3 (or_3_out, A, B);
  or or_4 (or_4_out, not_1_out, not_2_out);
  or or_5 (or_5_out, A, B);
  or or_6 (or_6_out, not_3_out, not_4_out);
  or or_7 (or_7_out, A, B);
  or or_8 (or_8_out, not_5_out, not_6_out);
  or or_9 (or_9_out, A, not_7_out);
  or or_10 (or_10_out, C, not_8_out);
  or or_11 (or_11_out, A, not_9_out);
  or or_12 (or_12_out, C, not_10_out);
  or or_13 (or_13_out, A, not_11_out);
  or or_14 (or_14_out, not_12_out, D);
  not not_33 (not_33_out, B);
  not not_34 (not_34_out, C);
  or or_15 (or_15_out, not_13_out, B);
  or or_16 (or_16_out, C, not_14_out);
  or or_17 (or_17_out, not_15_out, B);
  or or_18 (or_18_out, C, not_16_out);
  or or_19 (or_19_out, not_17_out, B);
  or or_20 (or_20_out, not_18_out, D);
  or or_21 (or_21_out, not_19_out, B);
  or or_22 (or_22_out, not_20_out, E);
  or or_23 (or_23_out, not_21_out, not_22_out);
  or or_24 (or_24_out, C, D);
  or or_25 (or_25_out, not_23_out, not_24_out);
  or or_26 (or_26_out, C, E);
  not not_35 (not_35_out, A);
  not not_36 (not_36_out, B);
  not not_37 (not_37_out, A);
  not not_38 (not_38_out, B);
  not not_39 (not_39_out, C);
  not not_40 (not_40_out, D);
  not not_41 (not_41_out, A);
  not not_42 (not_42_out, B);
  not not_43 (not_43_out, C);
  not not_44 (not_44_out, E);
  not not_45 (not_45_out, A);
  not not_46 (not_46_out, B);
  not not_47 (not_47_out, D);
  not not_48 (not_48_out, E);
  not not_49 (not_49_out, A);
  not not_50 (not_50_out, C);
  not not_51 (not_51_out, D);
  not not_52 (not_52_out, E);
  not not_53 (not_53_out, B);
  not not_54 (not_54_out, C);
  not not_55 (not_55_out, D);
  not not_56 (not_56_out, E);
  and and_11 (and_11_out, not_25_out, not_26_out);
  and and_12 (and_12_out, not_27_out, B);
  not not_57 (not_57_out, C);
  and and_13 (and_13_out, not_28_out, B);
  not not_58 (not_58_out, D);
  and and_14 (and_14_out, not_29_out, B);
  not not_59 (not_59_out, E);
  and and_15 (and_15_out, A, not_30_out);
  not not_60 (not_60_out, C);
  and and_16 (and_16_out, A, not_31_out);
  not not_61 (not_61_out, D);
  and and_17 (and_17_out, A, not_32_out);
  not not_62 (not_62_out, E);
  and and_18 (and_18_out, A, B);
  not not_63 (not_63_out, C);
  not not_64 (not_64_out, D);
  and and_19 (and_19_out, A, B);
  not not_65 (not_65_out, C);
  not not_66 (not_66_out, E);
  or or_27 (or_27_out, or_1_out, and_5_out);
  or or_28 (or_28_out, and_6_out, and_7_out);
  or or_29 (or_29_out, or_2_out, and_8_out);
  or or_30 (or_30_out, and_9_out, and_10_out);
  or or_31 (or_31_out, or_3_out, or_4_out);
  and and_20 (and_20_out, or_31_out, or_32_out);
  or or_32 (or_32_out, or_5_out, or_6_out);
  or or_33 (or_33_out, or_7_out, or_8_out);
  and and_21 (and_21_out, or_33_out, or_34_out);
  or or_34 (or_34_out, or_9_out, or_10_out);
  or or_35 (or_35_out, or_11_out, or_12_out);
  and and_22 (and_22_out, or_35_out, or_36_out);
  or or_36 (or_36_out, or_13_out, or_14_out);
  or or_37 (or_37_out, A, not_33_out);
  or or_38 (or_38_out, or_37_out, or_39_out);
  or or_39 (or_39_out, not_34_out, E);
  or or_40 (or_40_out, or_15_out, or_16_out);
  and and_23 (and_23_out, or_40_out, or_41_out);
  or or_41 (or_41_out, or_17_out, or_18_out);
  or or_42 (or_42_out, or_19_out, or_20_out);
  and and_24 (and_24_out, or_42_out, or_43_out);
  or or_43 (or_43_out, or_21_out, or_22_out);
  or or_44 (or_44_out, or_23_out, or_24_out);
  and and_25 (and_25_out, or_44_out, or_45_out);
  or or_45 (or_45_out, or_25_out, or_26_out);
  or or_46 (or_46_out, not_35_out, not_36_out);
  or or_47 (or_47_out, or_46_out, or_48_out);
  or or_48 (or_48_out, D, E);
  and and_26 (and_26_out, not_37_out, not_38_out);
  and and_27 (and_27_out, and_26_out, and_28_out);
  and and_28 (and_28_out, not_39_out, not_40_out);
  and and_29 (and_29_out, not_41_out, not_42_out);
  and and_30 (and_30_out, and_29_out, and_31_out);
  and and_31 (and_31_out, not_43_out, not_44_out);
  and and_32 (and_32_out, not_45_out, not_46_out);
  and and_33 (and_33_out, and_32_out, and_34_out);
  and and_34 (and_34_out, not_47_out, not_48_out);
  and and_35 (and_35_out, not_49_out, not_50_out);
  and and_36 (and_36_out, and_35_out, and_37_out);
  and and_37 (and_37_out, not_51_out, not_52_out);
  and and_38 (and_38_out, not_53_out, not_54_out);
  and and_39 (and_39_out, and_38_out, and_40_out);
  and and_40 (and_40_out, not_55_out, not_56_out);
  and and_41 (and_41_out, and_11_out, C);
  and and_42 (and_42_out, and_41_out, and_43_out);
  and and_43 (and_43_out, D, E);
  and and_44 (and_44_out, and_12_out, not_57_out);
  and and_45 (and_45_out, and_44_out, and_46_out);
  and and_46 (and_46_out, D, E);
  and and_47 (and_47_out, and_13_out, C);
  and and_48 (and_48_out, and_47_out, and_49_out);
  and and_49 (and_49_out, not_58_out, E);
  and and_50 (and_50_out, and_14_out, C);
  and and_51 (and_51_out, and_50_out, and_52_out);
  and and_52 (and_52_out, D, not_59_out);
  and and_53 (and_53_out, and_15_out, not_60_out);
  and and_54 (and_54_out, and_53_out, and_55_out);
  and and_55 (and_55_out, D, E);
  and and_56 (and_56_out, and_16_out, C);
  and and_57 (and_57_out, and_56_out, and_58_out);
  and and_58 (and_58_out, not_61_out, E);
  and and_59 (and_59_out, and_17_out, C);
  and and_60 (and_60_out, and_59_out, and_61_out);
  and and_61 (and_61_out, D, not_62_out);
  and and_62 (and_62_out, and_18_out, not_63_out);
  and and_63 (and_63_out, and_62_out, and_64_out);
  and and_64 (and_64_out, not_64_out, E);
  and and_65 (and_65_out, and_19_out, not_65_out);
  and and_66 (and_66_out, and_65_out, and_67_out);
  and and_67 (and_67_out, D, not_66_out);
  and and_68 (and_68_out, A, B);
  and and_69 (and_69_out, and_68_out, C);
  not not_67 (not_67_out, D);
  and and_70 (and_70_out, not_67_out, not_68_out);
  not not_68 (not_68_out, E);
  or or_49 (or_49_out, or_27_out, or_28_out);
  or or_50 (o1, or_49_out, or_51_out);
  or or_51 (or_51_out, or_29_out, or_30_out);
  and and_71 (and_71_out, and_20_out, and_21_out);
  and and_72 (and_72_out, and_22_out, or_38_out);
  and and_73 (and_73_out, and_23_out, and_24_out);
  and and_74 (and_74_out, and_25_out, or_47_out);
  or or_52 (or_52_out, and_27_out, and_30_out);
  or or_53 (or_53_out, and_33_out, and_36_out);
  or or_54 (or_54_out, and_39_out, and_42_out);
  or or_55 (or_55_out, and_45_out, and_48_out);
  or or_56 (or_56_out, and_51_out, and_54_out);
  or or_57 (or_57_out, and_57_out, and_60_out);
  or or_58 (or_58_out, and_63_out, and_66_out);
  and and_75 (and_75_out, and_69_out, and_70_out);
  and and_76 (and_76_out, and_71_out, and_72_out);
  and and_77 (and_77_out, and_73_out, and_74_out);
  or or_59 (or_59_out, or_52_out, or_53_out);
  or or_60 (or_60_out, or_54_out, or_55_out);
  or or_61 (or_61_out, or_56_out, or_57_out);
  or or_62 (or_62_out, or_58_out, and_75_out);
  and and_78 (o2, and_76_out, and_77_out);
  or or_63 (or_63_out, or_59_out, or_60_out);
  or or_64 (or_64_out, or_61_out, or_62_out);
  or or_65 (o3, or_63_out, or_64_out);
endmodule

module \_2_2_o2_min_з2__п1  (
  input  A,
  input  B,
  input  C,
  input  D,
  input  E,
  output o1,
  output o2,
  output o3
);

  wire and_1_out, and_2_out, and_3_out, and_4_out, and_5_out, and_6_out, and_7_out, and_8_out, and_9_out,
       and_10_out, and_11_out, and_12_out, and_13_out, and_14_out, and_15_out, and_16_out, and_17_out,
       and_18_out, and_19_out, and_20_out, and_21_out, and_22_out, and_23_out, and_24_out, and_25_out,
       and_26_out, and_27_out, and_28_out, and_29_out, and_30_out, and_31_out, and_32_out, and_33_out,
       and_34_out, and_35_out, and_36_out, and_37_out, and_38_out, and_39_out, and_40_out, and_41_out,
       and_42_out, and_43_out, and_44_out, and_45_out, and_46_out, and_47_out, and_48_out, and_49_out,
       and_50_out, and_51_out, and_52_out, and_53_out, and_54_out, and_55_out, and_56_out, and_57_out,
       and_58_out, and_59_out, and_60_out, and_61_out, and_62_out, and_63_out, and_64_out, and_65_out,
       and_66_out, and_67_out, and_68_out, and_69_out, and_70_out, and_71_out, and_72_out, and_73_out,
       and_74_out, and_75_out, and_76_out, and_77_out, and_78_out, and_79_out, and_80_out, and_81_out,
       and_82_out, and_83_out, and_84_out, and_85_out, and_86_out, and_87_out, and_88_out, and_89_out,
       and_90_out, and_91_out, and_92_out, and_93_out, and_94_out, and_95_out, not_1_out, not_2_out,
       not_3_out, not_4_out, not_5_out, not_6_out, not_7_out, not_8_out, not_9_out, not_10_out, not_11_out,
       not_12_out, not_13_out, not_14_out, not_15_out, not_16_out, not_17_out, not_18_out, not_19_out,
       not_20_out, not_21_out, not_22_out, not_23_out, not_24_out, not_25_out, not_26_out, not_27_out,
       not_28_out, not_29_out, not_30_out, not_31_out, not_32_out, not_33_out, not_34_out, not_35_out,
       not_36_out, not_37_out, not_38_out, not_39_out, not_40_out, not_41_out, not_42_out, not_43_out,
       not_44_out, not_45_out, not_46_out, not_47_out, not_48_out, not_49_out, not_50_out, not_51_out,
       not_52_out, not_53_out, not_54_out, not_55_out, not_56_out, not_57_out, not_58_out, not_59_out,
       not_60_out, or_1_out, or_2_out, or_3_out, or_4_out, or_5_out, or_6_out, or_7_out, or_8_out, or_9_out,
       or_11_out, or_12_out, or_13_out, or_14_out, or_15_out, or_16_out, or_17_out, or_18_out, or_19_out,
       or_20_out, or_21_out, or_22_out, or_23_out, or_24_out, or_25_out, or_26_out, or_27_out, or_28_out,
       or_30_out, or_31_out;

  and and_1 (and_1_out, D, E);
  and and_2 (and_2_out, C, E);
  and and_3 (and_3_out, B, C);
  and and_4 (and_4_out, A, E);
  not not_1 (not_1_out, A);
  not not_2 (not_2_out, B);
  not not_3 (not_3_out, C);
  not not_4 (not_4_out, D);
  not not_5 (not_5_out, A);
  not not_6 (not_6_out, B);
  not not_7 (not_7_out, C);
  not not_8 (not_8_out, E);
  not not_9 (not_9_out, A);
  not not_10 (not_10_out, B);
  not not_11 (not_11_out, A);
  not not_12 (not_12_out, A);
  not not_13 (not_13_out, A);
  not not_14 (not_14_out, B);
  not not_15 (not_15_out, B);
  not not_16 (not_16_out, B);
  or or_1 (or_1_out, and_1_out, and_2_out);
  and and_5 (and_5_out, C, D);
  and and_6 (and_6_out, B, E);
  and and_7 (and_7_out, B, D);
  or or_2 (or_2_out, and_3_out, and_4_out);
  and and_8 (and_8_out, A, D);
  and and_9 (and_9_out, A, C);
  and and_10 (and_10_out, A, B);
  and and_11 (and_11_out, not_1_out, not_2_out);
  and and_12 (and_12_out, not_3_out, not_4_out);
  and and_13 (and_13_out, not_5_out, not_6_out);
  and and_14 (and_14_out, not_7_out, not_8_out);
  not not_17 (not_17_out, A);
  not not_18 (not_18_out, B);
  not not_19 (not_19_out, D);
  not not_20 (not_20_out, E);
  not not_21 (not_21_out, A);
  not not_22 (not_22_out, C);
  not not_23 (not_23_out, D);
  not not_24 (not_24_out, E);
  not not_25 (not_25_out, B);
  not not_26 (not_26_out, C);
  not not_27 (not_27_out, D);
  not not_28 (not_28_out, E);
  and and_15 (and_15_out, B, C);
  and and_16 (and_16_out, D, E);
  and and_17 (and_17_out, A, C);
  and and_18 (and_18_out, D, E);
  not not_29 (not_29_out, A);
  not not_30 (not_30_out, B);
  not not_31 (not_31_out, C);
  not not_32 (not_32_out, D);
  not not_33 (not_33_out, A);
  not not_34 (not_34_out, B);
  not not_35 (not_35_out, C);
  not not_36 (not_36_out, E);
  not not_37 (not_37_out, A);
  not not_38 (not_38_out, B);
  not not_39 (not_39_out, D);
  not not_40 (not_40_out, E);
  not not_41 (not_41_out, A);
  not not_42 (not_42_out, C);
  not not_43 (not_43_out, D);
  not not_44 (not_44_out, E);
  not not_45 (not_45_out, B);
  not not_46 (not_46_out, C);
  not not_47 (not_47_out, D);
  not not_48 (not_48_out, E);
  and and_19 (and_19_out, not_9_out, not_10_out);
  and and_20 (and_20_out, not_11_out, B);
  not not_49 (not_49_out, C);
  and and_21 (and_21_out, not_12_out, B);
  not not_50 (not_50_out, D);
  and and_22 (and_22_out, not_13_out, B);
  not not_51 (not_51_out, E);
  and and_23 (and_23_out, A, not_14_out);
  not not_52 (not_52_out, C);
  and and_24 (and_24_out, A, not_15_out);
  not not_53 (not_53_out, D);
  and and_25 (and_25_out, A, not_16_out);
  not not_54 (not_54_out, E);
  and and_26 (and_26_out, A, B);
  not not_55 (not_55_out, C);
  not not_56 (not_56_out, D);
  and and_27 (and_27_out, A, B);
  not not_57 (not_57_out, C);
  not not_58 (not_58_out, E);
  or or_3 (or_3_out, or_1_out, and_5_out);
  or or_4 (or_4_out, and_6_out, and_7_out);
  or or_5 (or_5_out, or_2_out, and_8_out);
  or or_6 (or_6_out, and_9_out, and_10_out);
  and and_28 (and_28_out, and_11_out, and_12_out);
  or or_7 (or_7_out, and_28_out, and_29_out);
  and and_29 (and_29_out, and_13_out, and_14_out);
  and and_30 (and_30_out, not_17_out, not_18_out);
  and and_31 (and_31_out, and_30_out, and_32_out);
  and and_32 (and_32_out, not_19_out, not_20_out);
  and and_33 (and_33_out, not_21_out, not_22_out);
  and and_34 (and_34_out, and_33_out, and_35_out);
  and and_35 (and_35_out, not_23_out, not_24_out);
  and and_36 (and_36_out, not_25_out, not_26_out);
  and and_37 (and_37_out, and_36_out, and_38_out);
  and and_38 (and_38_out, not_27_out, not_28_out);
  and and_39 (and_39_out, and_15_out, and_16_out);
  or or_8 (or_8_out, and_39_out, and_40_out);
  and and_40 (and_40_out, and_17_out, and_18_out);
  and and_41 (and_41_out, A, B);
  and and_42 (and_42_out, and_41_out, and_43_out);
  and and_43 (and_43_out, D, E);
  and and_44 (and_44_out, A, B);
  and and_45 (and_45_out, and_44_out, and_46_out);
  and and_46 (and_46_out, C, E);
  and and_47 (and_47_out, A, B);
  and and_48 (and_48_out, and_47_out, and_49_out);
  and and_49 (and_49_out, C, D);
  and and_50 (and_50_out, not_29_out, not_30_out);
  and and_51 (and_51_out, and_50_out, and_52_out);
  and and_52 (and_52_out, not_31_out, not_32_out);
  and and_53 (and_53_out, not_33_out, not_34_out);
  and and_54 (and_54_out, and_53_out, and_55_out);
  and and_55 (and_55_out, not_35_out, not_36_out);
  and and_56 (and_56_out, not_37_out, not_38_out);
  and and_57 (and_57_out, and_56_out, and_58_out);
  and and_58 (and_58_out, not_39_out, not_40_out);
  and and_59 (and_59_out, not_41_out, not_42_out);
  and and_60 (and_60_out, and_59_out, and_61_out);
  and and_61 (and_61_out, not_43_out, not_44_out);
  and and_62 (and_62_out, not_45_out, not_46_out);
  and and_63 (and_63_out, and_62_out, and_64_out);
  and and_64 (and_64_out, not_47_out, not_48_out);
  and and_65 (and_65_out, and_19_out, C);
  and and_66 (and_66_out, and_65_out, and_67_out);
  and and_67 (and_67_out, D, E);
  and and_68 (and_68_out, and_20_out, not_49_out);
  and and_69 (and_69_out, and_68_out, and_70_out);
  and and_70 (and_70_out, D, E);
  and and_71 (and_71_out, and_21_out, C);
  and and_72 (and_72_out, and_71_out, and_73_out);
  and and_73 (and_73_out, not_50_out, E);
  and and_74 (and_74_out, and_22_out, C);
  and and_75 (and_75_out, and_74_out, and_76_out);
  and and_76 (and_76_out, D, not_51_out);
  and and_77 (and_77_out, and_23_out, not_52_out);
  and and_78 (and_78_out, and_77_out, and_79_out);
  and and_79 (and_79_out, D, E);
  and and_80 (and_80_out, and_24_out, C);
  and and_81 (and_81_out, and_80_out, and_82_out);
  and and_82 (and_82_out, not_53_out, E);
  and and_83 (and_83_out, and_25_out, C);
  and and_84 (and_84_out, and_83_out, and_85_out);
  and and_85 (and_85_out, D, not_54_out);
  and and_86 (and_86_out, and_26_out, not_55_out);
  and and_87 (and_87_out, and_86_out, and_88_out);
  and and_88 (and_88_out, not_56_out, E);
  and and_89 (and_89_out, and_27_out, not_57_out);
  and and_90 (and_90_out, and_89_out, and_91_out);
  and and_91 (and_91_out, D, not_58_out);
  and and_92 (and_92_out, A, B);
  and and_93 (and_93_out, and_92_out, C);
  not not_59 (not_59_out, D);
  and and_94 (and_94_out, not_59_out, not_60_out);
  not not_60 (not_60_out, E);
  or or_9 (or_9_out, or_3_out, or_4_out);
  or or_10 (o1, or_9_out, or_11_out);
  or or_11 (or_11_out, or_5_out, or_6_out);
  or or_12 (or_12_out, or_7_out, and_31_out);
  or or_13 (or_13_out, and_34_out, and_37_out);
  or or_14 (or_14_out, or_8_out, and_42_out);
  or or_15 (or_15_out, and_45_out, and_48_out);
  or or_16 (or_16_out, and_51_out, and_54_out);
  or or_17 (or_17_out, and_57_out, and_60_out);
  or or_18 (or_18_out, and_63_out, and_66_out);
  or or_19 (or_19_out, and_69_out, and_72_out);
  or or_20 (or_20_out, and_75_out, and_78_out);
  or or_21 (or_21_out, and_81_out, and_84_out);
  or or_22 (or_22_out, and_87_out, and_90_out);
  and and_95 (and_95_out, and_93_out, and_94_out);
  or or_23 (or_23_out, or_12_out, or_13_out);
  or or_24 (or_24_out, or_14_out, or_15_out);
  or or_25 (or_25_out, or_16_out, or_17_out);
  or or_26 (or_26_out, or_18_out, or_19_out);
  or or_27 (or_27_out, or_20_out, or_21_out);
  or or_28 (or_28_out, or_22_out, and_95_out);
  or or_29 (o2, or_23_out, or_24_out);
  or or_30 (or_30_out, or_25_out, or_26_out);
  or or_31 (or_31_out, or_27_out, or_28_out);
  or or_32 (o3, or_30_out, or_31_out);
endmodule

module \_2_2_o3_min_з2__п1  (
  input  A,
  input  B,
  input  C,
  input  D,
  input  E,
  output o1,
  output o2,
  output o3
);

  wire and_1_out, and_2_out, and_3_out, and_4_out, and_5_out, and_6_out, and_7_out, and_8_out, and_9_out,
       and_10_out, and_11_out, and_12_out, and_13_out, and_14_out, and_15_out, and_16_out, and_17_out,
       and_18_out, and_19_out, and_20_out, and_21_out, and_22_out, and_23_out, and_24_out, and_25_out,
       and_26_out, and_27_out, and_28_out, and_29_out, and_30_out, and_31_out, and_32_out, and_33_out,
       and_34_out, and_35_out, and_36_out, and_37_out, and_38_out, and_39_out, and_40_out, and_41_out,
       and_42_out, and_43_out, and_44_out, and_45_out, and_46_out, and_47_out, and_48_out, and_49_out,
       and_50_out, and_51_out, and_52_out, and_53_out, and_54_out, and_55_out, and_56_out, and_57_out,
       and_58_out, and_59_out, and_60_out, and_61_out, and_62_out, and_63_out, and_64_out, and_65_out,
       and_66_out, and_67_out, and_68_out, and_69_out, and_70_out, and_71_out, and_72_out, and_73_out,
       and_74_out, and_75_out, and_76_out, and_77_out, and_78_out, and_79_out, and_80_out, and_81_out,
       and_82_out, and_83_out, and_84_out, and_85_out, and_86_out, and_87_out, and_88_out, and_89_out,
       and_90_out, and_91_out, and_92_out, and_93_out, and_94_out, and_95_out, not_1_out, not_2_out,
       not_3_out, not_4_out, not_5_out, not_6_out, not_7_out, not_8_out, not_9_out, not_10_out, not_11_out,
       not_12_out, not_13_out, not_14_out, not_15_out, not_16_out, not_17_out, not_18_out, not_19_out,
       not_20_out, not_21_out, not_22_out, not_23_out, not_24_out, not_25_out, not_26_out, not_27_out,
       not_28_out, not_29_out, not_30_out, not_31_out, not_32_out, not_33_out, not_34_out, not_35_out,
       not_36_out, not_37_out, not_38_out, not_39_out, not_40_out, not_41_out, not_42_out, not_43_out,
       not_44_out, not_45_out, not_46_out, not_47_out, not_48_out, not_49_out, not_50_out, not_51_out,
       not_52_out, not_53_out, not_54_out, not_55_out, not_56_out, not_57_out, not_58_out, not_59_out,
       not_60_out, or_1_out, or_2_out, or_3_out, or_4_out, or_5_out, or_6_out, or_7_out, or_8_out, or_9_out,
       or_11_out, or_12_out, or_13_out, or_14_out, or_15_out, or_16_out, or_17_out, or_18_out, or_19_out,
       or_20_out, or_21_out, or_22_out, or_23_out, or_24_out, or_25_out, or_26_out, or_27_out, or_28_out,
       or_30_out, or_31_out;

  and and_1 (and_1_out, D, E);
  and and_2 (and_2_out, C, E);
  and and_3 (and_3_out, B, C);
  and and_4 (and_4_out, A, E);
  not not_1 (not_1_out, A);
  not not_2 (not_2_out, B);
  not not_3 (not_3_out, C);
  not not_4 (not_4_out, D);
  not not_5 (not_5_out, A);
  not not_6 (not_6_out, B);
  not not_7 (not_7_out, C);
  not not_8 (not_8_out, E);
  not not_9 (not_9_out, A);
  not not_10 (not_10_out, B);
  not not_11 (not_11_out, A);
  not not_12 (not_12_out, A);
  not not_13 (not_13_out, A);
  not not_14 (not_14_out, B);
  not not_15 (not_15_out, B);
  not not_16 (not_16_out, B);
  or or_1 (or_1_out, and_1_out, and_2_out);
  and and_5 (and_5_out, C, D);
  and and_6 (and_6_out, B, E);
  and and_7 (and_7_out, B, D);
  or or_2 (or_2_out, and_3_out, and_4_out);
  and and_8 (and_8_out, A, D);
  and and_9 (and_9_out, A, C);
  and and_10 (and_10_out, A, B);
  and and_11 (and_11_out, not_1_out, not_2_out);
  and and_12 (and_12_out, not_3_out, not_4_out);
  and and_13 (and_13_out, not_5_out, not_6_out);
  and and_14 (and_14_out, not_7_out, not_8_out);
  not not_17 (not_17_out, A);
  not not_18 (not_18_out, B);
  not not_19 (not_19_out, D);
  not not_20 (not_20_out, E);
  not not_21 (not_21_out, A);
  not not_22 (not_22_out, C);
  not not_23 (not_23_out, D);
  not not_24 (not_24_out, E);
  not not_25 (not_25_out, B);
  not not_26 (not_26_out, C);
  not not_27 (not_27_out, D);
  not not_28 (not_28_out, E);
  and and_15 (and_15_out, B, C);
  and and_16 (and_16_out, D, E);
  and and_17 (and_17_out, A, C);
  and and_18 (and_18_out, D, E);
  not not_29 (not_29_out, A);
  not not_30 (not_30_out, B);
  not not_31 (not_31_out, C);
  not not_32 (not_32_out, D);
  not not_33 (not_33_out, A);
  not not_34 (not_34_out, B);
  not not_35 (not_35_out, C);
  not not_36 (not_36_out, E);
  not not_37 (not_37_out, A);
  not not_38 (not_38_out, B);
  not not_39 (not_39_out, D);
  not not_40 (not_40_out, E);
  not not_41 (not_41_out, A);
  not not_42 (not_42_out, C);
  not not_43 (not_43_out, D);
  not not_44 (not_44_out, E);
  not not_45 (not_45_out, B);
  not not_46 (not_46_out, C);
  not not_47 (not_47_out, D);
  not not_48 (not_48_out, E);
  and and_19 (and_19_out, not_9_out, not_10_out);
  and and_20 (and_20_out, not_11_out, B);
  not not_49 (not_49_out, C);
  and and_21 (and_21_out, not_12_out, B);
  not not_50 (not_50_out, D);
  and and_22 (and_22_out, not_13_out, B);
  not not_51 (not_51_out, E);
  and and_23 (and_23_out, A, not_14_out);
  not not_52 (not_52_out, C);
  and and_24 (and_24_out, A, not_15_out);
  not not_53 (not_53_out, D);
  and and_25 (and_25_out, A, not_16_out);
  not not_54 (not_54_out, E);
  and and_26 (and_26_out, A, B);
  not not_55 (not_55_out, C);
  not not_56 (not_56_out, D);
  and and_27 (and_27_out, A, B);
  not not_57 (not_57_out, C);
  not not_58 (not_58_out, E);
  or or_3 (or_3_out, or_1_out, and_5_out);
  or or_4 (or_4_out, and_6_out, and_7_out);
  or or_5 (or_5_out, or_2_out, and_8_out);
  or or_6 (or_6_out, and_9_out, and_10_out);
  and and_28 (and_28_out, and_11_out, and_12_out);
  or or_7 (or_7_out, and_28_out, and_29_out);
  and and_29 (and_29_out, and_13_out, and_14_out);
  and and_30 (and_30_out, not_17_out, not_18_out);
  and and_31 (and_31_out, and_30_out, and_32_out);
  and and_32 (and_32_out, not_19_out, not_20_out);
  and and_33 (and_33_out, not_21_out, not_22_out);
  and and_34 (and_34_out, and_33_out, and_35_out);
  and and_35 (and_35_out, not_23_out, not_24_out);
  and and_36 (and_36_out, not_25_out, not_26_out);
  and and_37 (and_37_out, and_36_out, and_38_out);
  and and_38 (and_38_out, not_27_out, not_28_out);
  and and_39 (and_39_out, and_15_out, and_16_out);
  or or_8 (or_8_out, and_39_out, and_40_out);
  and and_40 (and_40_out, and_17_out, and_18_out);
  and and_41 (and_41_out, A, B);
  and and_42 (and_42_out, and_41_out, and_43_out);
  and and_43 (and_43_out, D, E);
  and and_44 (and_44_out, A, B);
  and and_45 (and_45_out, and_44_out, and_46_out);
  and and_46 (and_46_out, C, E);
  and and_47 (and_47_out, A, B);
  and and_48 (and_48_out, and_47_out, and_49_out);
  and and_49 (and_49_out, C, D);
  and and_50 (and_50_out, not_29_out, not_30_out);
  and and_51 (and_51_out, and_50_out, and_52_out);
  and and_52 (and_52_out, not_31_out, not_32_out);
  and and_53 (and_53_out, not_33_out, not_34_out);
  and and_54 (and_54_out, and_53_out, and_55_out);
  and and_55 (and_55_out, not_35_out, not_36_out);
  and and_56 (and_56_out, not_37_out, not_38_out);
  and and_57 (and_57_out, and_56_out, and_58_out);
  and and_58 (and_58_out, not_39_out, not_40_out);
  and and_59 (and_59_out, not_41_out, not_42_out);
  and and_60 (and_60_out, and_59_out, and_61_out);
  and and_61 (and_61_out, not_43_out, not_44_out);
  and and_62 (and_62_out, not_45_out, not_46_out);
  and and_63 (and_63_out, and_62_out, and_64_out);
  and and_64 (and_64_out, not_47_out, not_48_out);
  and and_65 (and_65_out, and_19_out, C);
  and and_66 (and_66_out, and_65_out, and_67_out);
  and and_67 (and_67_out, D, E);
  and and_68 (and_68_out, and_20_out, not_49_out);
  and and_69 (and_69_out, and_68_out, and_70_out);
  and and_70 (and_70_out, D, E);
  and and_71 (and_71_out, and_21_out, C);
  and and_72 (and_72_out, and_71_out, and_73_out);
  and and_73 (and_73_out, not_50_out, E);
  and and_74 (and_74_out, and_22_out, C);
  and and_75 (and_75_out, and_74_out, and_76_out);
  and and_76 (and_76_out, D, not_51_out);
  and and_77 (and_77_out, and_23_out, not_52_out);
  and and_78 (and_78_out, and_77_out, and_79_out);
  and and_79 (and_79_out, D, E);
  and and_80 (and_80_out, and_24_out, C);
  and and_81 (and_81_out, and_80_out, and_82_out);
  and and_82 (and_82_out, not_53_out, E);
  and and_83 (and_83_out, and_25_out, C);
  and and_84 (and_84_out, and_83_out, and_85_out);
  and and_85 (and_85_out, D, not_54_out);
  and and_86 (and_86_out, and_26_out, not_55_out);
  and and_87 (and_87_out, and_86_out, and_88_out);
  and and_88 (and_88_out, not_56_out, E);
  and and_89 (and_89_out, and_27_out, not_57_out);
  and and_90 (and_90_out, and_89_out, and_91_out);
  and and_91 (and_91_out, D, not_58_out);
  and and_92 (and_92_out, A, B);
  and and_93 (and_93_out, and_92_out, C);
  not not_59 (not_59_out, D);
  and and_94 (and_94_out, not_59_out, not_60_out);
  not not_60 (not_60_out, E);
  or or_9 (or_9_out, or_3_out, or_4_out);
  or or_10 (o1, or_9_out, or_11_out);
  or or_11 (or_11_out, or_5_out, or_6_out);
  or or_12 (or_12_out, or_7_out, and_31_out);
  or or_13 (or_13_out, and_34_out, and_37_out);
  or or_14 (or_14_out, or_8_out, and_42_out);
  or or_15 (or_15_out, and_45_out, and_48_out);
  or or_16 (or_16_out, and_51_out, and_54_out);
  or or_17 (or_17_out, and_57_out, and_60_out);
  or or_18 (or_18_out, and_63_out, and_66_out);
  or or_19 (or_19_out, and_69_out, and_72_out);
  or or_20 (or_20_out, and_75_out, and_78_out);
  or or_21 (or_21_out, and_81_out, and_84_out);
  or or_22 (or_22_out, and_87_out, and_90_out);
  and and_95 (and_95_out, and_93_out, and_94_out);
  or or_23 (or_23_out, or_12_out, or_13_out);
  or or_24 (or_24_out, or_14_out, or_15_out);
  or or_25 (or_25_out, or_16_out, or_17_out);
  or or_26 (or_26_out, or_18_out, or_19_out);
  or or_27 (or_27_out, or_20_out, or_21_out);
  or or_28 (or_28_out, or_22_out, and_95_out);
  or or_29 (o2, or_23_out, or_24_out);
  or or_30 (or_30_out, or_25_out, or_26_out);
  or or_31 (or_31_out, or_27_out, or_28_out);
  or or_32 (o3, or_30_out, or_31_out);
endmodule

module \задание_2__пункт_2___logicfriday  (
  input  A,
  input  B,
  input  C,
  input  D,
  input  E,
  output o1,
  output o2,
  output o3
);

  wire and_1_out, and_2_out, and_3_out, and_4_out, and_5_out, and_6_out, and_7_out, and_8_out, and_9_out,
       and_10_out, and_11_out, and_12_out, and_13_out, and_14_out, and_15_out, and_16_out, and_17_out,
       and_18_out, and_19_out, and_20_out, and_21_out, and_22_out, and_23_out, and_24_out, and_25_out,
       and_26_out, and_27_out, and_28_out, and_29_out, and_30_out, and_31_out, and_32_out, and_33_out,
       and_34_out, and_35_out, and_36_out, and_37_out, and_38_out, and_39_out, and_40_out, and_41_out,
       and_42_out, and_43_out, and_44_out, and_45_out, and_46_out, and_47_out, and_48_out, and_49_out,
       and_50_out, and_51_out, and_52_out, and_53_out, and_54_out, and_55_out, and_56_out, and_57_out,
       and_58_out, and_59_out, and_60_out, and_61_out, and_62_out, and_63_out, and_64_out, and_65_out,
       and_66_out, and_67_out, and_68_out, and_69_out, and_70_out, and_71_out, and_72_out, and_73_out,
       and_74_out, and_75_out, and_76_out, and_77_out, and_78_out, and_79_out, and_80_out, and_81_out,
       and_82_out, and_83_out, and_84_out, and_85_out, and_86_out, and_87_out, and_88_out, and_89_out,
       and_90_out, and_91_out, and_92_out, and_93_out, and_94_out, and_95_out, not_1_out, not_2_out,
       not_3_out, not_4_out, not_5_out, not_6_out, not_7_out, not_8_out, not_9_out, not_10_out, not_11_out,
       not_12_out, not_13_out, not_14_out, not_15_out, not_16_out, not_17_out, not_18_out, not_19_out,
       not_20_out, not_21_out, not_22_out, not_23_out, not_24_out, not_25_out, not_26_out, not_27_out,
       not_28_out, not_29_out, not_30_out, not_31_out, not_32_out, not_33_out, not_34_out, not_35_out,
       not_36_out, not_37_out, not_38_out, not_39_out, not_40_out, not_41_out, not_42_out, not_43_out,
       not_44_out, not_45_out, not_46_out, not_47_out, not_48_out, not_49_out, not_50_out, not_51_out,
       not_52_out, not_53_out, not_54_out, not_55_out, not_56_out, not_57_out, not_58_out, not_59_out,
       not_60_out, or_1_out, or_2_out, or_3_out, or_4_out, or_5_out, or_6_out, or_7_out, or_8_out, or_9_out,
       or_11_out, or_12_out, or_13_out, or_14_out, or_15_out, or_16_out, or_17_out, or_18_out, or_19_out,
       or_20_out, or_21_out, or_22_out, or_23_out, or_24_out, or_25_out, or_26_out, or_27_out, or_28_out,
       or_30_out, or_31_out;

  and and_1 (and_1_out, A, B);
  and and_2 (and_2_out, A, C);
  and and_3 (and_3_out, C, D);
  and and_4 (and_4_out, A, E);
  not not_1 (not_1_out, A);
  not not_2 (not_2_out, B);
  not not_3 (not_3_out, C);
  not not_4 (not_4_out, D);
  not not_5 (not_5_out, A);
  not not_6 (not_6_out, B);
  not not_7 (not_7_out, C);
  not not_8 (not_8_out, E);
  not not_9 (not_9_out, A);
  not not_10 (not_10_out, B);
  not not_11 (not_11_out, A);
  not not_12 (not_12_out, A);
  not not_13 (not_13_out, A);
  not not_14 (not_14_out, B);
  not not_15 (not_15_out, B);
  not not_16 (not_16_out, B);
  or or_1 (or_1_out, and_1_out, and_2_out);
  and and_5 (and_5_out, B, C);
  and and_6 (and_6_out, A, D);
  and and_7 (and_7_out, B, D);
  or or_2 (or_2_out, and_3_out, and_4_out);
  and and_8 (and_8_out, B, E);
  and and_9 (and_9_out, C, E);
  and and_10 (and_10_out, D, E);
  and and_11 (and_11_out, not_1_out, not_2_out);
  and and_12 (and_12_out, not_3_out, not_4_out);
  and and_13 (and_13_out, not_5_out, not_6_out);
  and and_14 (and_14_out, not_7_out, not_8_out);
  not not_17 (not_17_out, A);
  not not_18 (not_18_out, B);
  not not_19 (not_19_out, D);
  not not_20 (not_20_out, E);
  not not_21 (not_21_out, A);
  not not_22 (not_22_out, C);
  not not_23 (not_23_out, D);
  not not_24 (not_24_out, E);
  not not_25 (not_25_out, B);
  not not_26 (not_26_out, C);
  not not_27 (not_27_out, D);
  not not_28 (not_28_out, E);
  and and_15 (and_15_out, B, C);
  and and_16 (and_16_out, D, E);
  and and_17 (and_17_out, A, C);
  and and_18 (and_18_out, D, E);
  not not_29 (not_29_out, A);
  not not_30 (not_30_out, B);
  not not_31 (not_31_out, C);
  not not_32 (not_32_out, D);
  not not_33 (not_33_out, A);
  not not_34 (not_34_out, B);
  not not_35 (not_35_out, C);
  not not_36 (not_36_out, E);
  not not_37 (not_37_out, A);
  not not_38 (not_38_out, B);
  not not_39 (not_39_out, D);
  not not_40 (not_40_out, E);
  not not_41 (not_41_out, A);
  not not_42 (not_42_out, C);
  not not_43 (not_43_out, D);
  not not_44 (not_44_out, E);
  not not_45 (not_45_out, B);
  not not_46 (not_46_out, C);
  not not_47 (not_47_out, D);
  not not_48 (not_48_out, E);
  and and_19 (and_19_out, not_9_out, not_10_out);
  and and_20 (and_20_out, not_11_out, B);
  not not_49 (not_49_out, C);
  and and_21 (and_21_out, not_12_out, B);
  not not_50 (not_50_out, D);
  and and_22 (and_22_out, not_13_out, B);
  not not_51 (not_51_out, E);
  and and_23 (and_23_out, A, not_14_out);
  not not_52 (not_52_out, C);
  and and_24 (and_24_out, A, not_15_out);
  not not_53 (not_53_out, D);
  and and_25 (and_25_out, A, not_16_out);
  not not_54 (not_54_out, E);
  and and_26 (and_26_out, A, B);
  not not_55 (not_55_out, C);
  not not_56 (not_56_out, D);
  and and_27 (and_27_out, A, B);
  not not_57 (not_57_out, C);
  not not_58 (not_58_out, E);
  or or_3 (or_3_out, or_1_out, and_5_out);
  or or_4 (or_4_out, and_6_out, and_7_out);
  or or_5 (or_5_out, or_2_out, and_8_out);
  or or_6 (or_6_out, and_9_out, and_10_out);
  and and_28 (and_28_out, and_11_out, and_12_out);
  or or_7 (or_7_out, and_28_out, and_29_out);
  and and_29 (and_29_out, and_13_out, and_14_out);
  and and_30 (and_30_out, not_17_out, not_18_out);
  and and_31 (and_31_out, and_30_out, and_32_out);
  and and_32 (and_32_out, not_19_out, not_20_out);
  and and_33 (and_33_out, not_21_out, not_22_out);
  and and_34 (and_34_out, and_33_out, and_35_out);
  and and_35 (and_35_out, not_23_out, not_24_out);
  and and_36 (and_36_out, not_25_out, not_26_out);
  and and_37 (and_37_out, and_36_out, and_38_out);
  and and_38 (and_38_out, not_27_out, not_28_out);
  and and_39 (and_39_out, and_15_out, and_16_out);
  or or_8 (or_8_out, and_39_out, and_40_out);
  and and_40 (and_40_out, and_17_out, and_18_out);
  and and_41 (and_41_out, A, B);
  and and_42 (and_42_out, and_41_out, and_43_out);
  and and_43 (and_43_out, D, E);
  and and_44 (and_44_out, A, B);
  and and_45 (and_45_out, and_44_out, and_46_out);
  and and_46 (and_46_out, C, E);
  and and_47 (and_47_out, A, B);
  and and_48 (and_48_out, and_47_out, and_49_out);
  and and_49 (and_49_out, C, D);
  and and_50 (and_50_out, not_29_out, not_30_out);
  and and_51 (and_51_out, and_50_out, and_52_out);
  and and_52 (and_52_out, not_31_out, not_32_out);
  and and_53 (and_53_out, not_33_out, not_34_out);
  and and_54 (and_54_out, and_53_out, and_55_out);
  and and_55 (and_55_out, not_35_out, not_36_out);
  and and_56 (and_56_out, not_37_out, not_38_out);
  and and_57 (and_57_out, and_56_out, and_58_out);
  and and_58 (and_58_out, not_39_out, not_40_out);
  and and_59 (and_59_out, not_41_out, not_42_out);
  and and_60 (and_60_out, and_59_out, and_61_out);
  and and_61 (and_61_out, not_43_out, not_44_out);
  and and_62 (and_62_out, not_45_out, not_46_out);
  and and_63 (and_63_out, and_62_out, and_64_out);
  and and_64 (and_64_out, not_47_out, not_48_out);
  and and_65 (and_65_out, and_19_out, C);
  and and_66 (and_66_out, and_65_out, and_67_out);
  and and_67 (and_67_out, D, E);
  and and_68 (and_68_out, and_20_out, not_49_out);
  and and_69 (and_69_out, and_68_out, and_70_out);
  and and_70 (and_70_out, D, E);
  and and_71 (and_71_out, and_21_out, C);
  and and_72 (and_72_out, and_71_out, and_73_out);
  and and_73 (and_73_out, not_50_out, E);
  and and_74 (and_74_out, and_22_out, C);
  and and_75 (and_75_out, and_74_out, and_76_out);
  and and_76 (and_76_out, D, not_51_out);
  and and_77 (and_77_out, and_23_out, not_52_out);
  and and_78 (and_78_out, and_77_out, and_79_out);
  and and_79 (and_79_out, D, E);
  and and_80 (and_80_out, and_24_out, C);
  and and_81 (and_81_out, and_80_out, and_82_out);
  and and_82 (and_82_out, not_53_out, E);
  and and_83 (and_83_out, and_25_out, C);
  and and_84 (and_84_out, and_83_out, and_85_out);
  and and_85 (and_85_out, D, not_54_out);
  and and_86 (and_86_out, and_26_out, not_55_out);
  and and_87 (and_87_out, and_86_out, and_88_out);
  and and_88 (and_88_out, not_56_out, E);
  and and_89 (and_89_out, and_27_out, not_57_out);
  and and_90 (and_90_out, and_89_out, and_91_out);
  and and_91 (and_91_out, D, not_58_out);
  and and_92 (and_92_out, A, B);
  and and_93 (and_93_out, and_92_out, C);
  not not_59 (not_59_out, D);
  and and_94 (and_94_out, not_59_out, not_60_out);
  not not_60 (not_60_out, E);
  or or_9 (or_9_out, or_3_out, or_4_out);
  or or_10 (o1, or_9_out, or_11_out);
  or or_11 (or_11_out, or_5_out, or_6_out);
  or or_12 (or_12_out, or_7_out, and_31_out);
  or or_13 (or_13_out, and_34_out, and_37_out);
  or or_14 (or_14_out, or_8_out, and_42_out);
  or or_15 (or_15_out, and_45_out, and_48_out);
  or or_16 (or_16_out, and_51_out, and_54_out);
  or or_17 (or_17_out, and_57_out, and_60_out);
  or or_18 (or_18_out, and_63_out, and_66_out);
  or or_19 (or_19_out, and_69_out, and_72_out);
  or or_20 (or_20_out, and_75_out, and_78_out);
  or or_21 (or_21_out, and_81_out, and_84_out);
  or or_22 (or_22_out, and_87_out, and_90_out);
  and and_95 (and_95_out, and_93_out, and_94_out);
  or or_23 (or_23_out, or_12_out, or_13_out);
  or or_24 (or_24_out, or_14_out, or_15_out);
  or or_25 (or_25_out, or_16_out, or_17_out);
  or or_26 (or_26_out, or_18_out, or_19_out);
  or or_27 (or_27_out, or_20_out, or_21_out);
  or or_28 (or_28_out, or_22_out, and_95_out);
  or or_29 (o2, or_23_out, or_24_out);
  or or_30 (or_30_out, or_25_out, or_26_out);
  or or_31 (or_31_out, or_27_out, or_28_out);
  or or_32 (o3, or_30_out, or_31_out);
endmodule
module \задание_2__пункт_2__logicfriday__o2  (
  input  A,
  input  B,
  input  C,
  input  D,
  input  E,
  output o1,
  output o2,
  output o3
);

  wire and_1_out, and_2_out, and_3_out, and_4_out, and_5_out, and_6_out, and_7_out, and_8_out, and_9_out,
       and_10_out, and_11_out, and_12_out, and_13_out, and_14_out, and_15_out, and_16_out, and_17_out,
       and_18_out, and_19_out, and_20_out, and_21_out, and_22_out, and_23_out, and_24_out, and_25_out,
       and_26_out, and_27_out, and_28_out, and_29_out, and_30_out, and_31_out, and_32_out, and_33_out,
       and_34_out, and_35_out, and_36_out, and_37_out, and_38_out, and_39_out, and_40_out, and_41_out,
       and_42_out, and_43_out, and_44_out, and_45_out, and_46_out, and_47_out, and_48_out, and_49_out,
       and_50_out, and_51_out, and_52_out, and_53_out, and_54_out, and_55_out, and_56_out, and_57_out,
       and_58_out, and_59_out, and_60_out, and_61_out, and_62_out, and_63_out, and_64_out, and_65_out,
       and_66_out, and_67_out, and_68_out, and_69_out, and_70_out, and_71_out, and_72_out, and_73_out,
       and_74_out, and_75_out, and_76_out, and_77_out, and_78_out, and_79_out, and_80_out, and_81_out,
       and_82_out, and_83_out, and_84_out, and_85_out, and_86_out, and_87_out, and_88_out, and_89_out,
       and_90_out, and_91_out, and_92_out, and_93_out, and_94_out, and_95_out, not_1_out, not_2_out,
       not_3_out, not_4_out, not_5_out, not_6_out, not_7_out, not_8_out, not_9_out, not_10_out, not_11_out,
       not_12_out, not_13_out, not_14_out, not_15_out, not_16_out, not_17_out, not_18_out, not_19_out,
       not_20_out, not_21_out, not_22_out, not_23_out, not_24_out, not_25_out, not_26_out, not_27_out,
       not_28_out, not_29_out, not_30_out, not_31_out, not_32_out, not_33_out, not_34_out, not_35_out,
       not_36_out, not_37_out, not_38_out, not_39_out, not_40_out, not_41_out, not_42_out, not_43_out,
       not_44_out, not_45_out, not_46_out, not_47_out, not_48_out, not_49_out, not_50_out, not_51_out,
       not_52_out, not_53_out, not_54_out, not_55_out, not_56_out, not_57_out, not_58_out, not_59_out,
       not_60_out, or_1_out, or_2_out, or_3_out, or_4_out, or_5_out, or_6_out, or_7_out, or_8_out, or_9_out,
       or_11_out, or_12_out, or_13_out, or_14_out, or_15_out, or_16_out, or_17_out, or_18_out, or_19_out,
       or_20_out, or_21_out, or_22_out, or_23_out, or_24_out, or_25_out, or_26_out, or_27_out, or_28_out,
       or_30_out, or_31_out;

  and and_1 (and_1_out, A, B);
  and and_2 (and_2_out, A, C);
  and and_3 (and_3_out, C, D);
  and and_4 (and_4_out, A, E);
  not not_1 (not_1_out, A);
  not not_2 (not_2_out, B);
  not not_3 (not_3_out, C);
  not not_4 (not_4_out, D);
  not not_5 (not_5_out, A);
  not not_6 (not_6_out, B);
  not not_7 (not_7_out, C);
  not not_8 (not_8_out, E);
  not not_9 (not_9_out, A);
  not not_10 (not_10_out, B);
  not not_11 (not_11_out, A);
  not not_12 (not_12_out, A);
  not not_13 (not_13_out, A);
  not not_14 (not_14_out, B);
  not not_15 (not_15_out, B);
  not not_16 (not_16_out, B);
  or or_1 (or_1_out, and_1_out, and_2_out);
  and and_5 (and_5_out, B, C);
  and and_6 (and_6_out, A, D);
  and and_7 (and_7_out, B, D);
  or or_2 (or_2_out, and_3_out, and_4_out);
  and and_8 (and_8_out, B, E);
  and and_9 (and_9_out, C, E);
  and and_10 (and_10_out, D, E);
  and and_11 (and_11_out, A, B);
  and and_12 (and_12_out, C, D);
  and and_13 (and_13_out, not_1_out, not_2_out);
  and and_14 (and_14_out, not_3_out, not_4_out);
  and and_15 (and_15_out, B, C);
  and and_16 (and_16_out, D, E);
  and and_17 (and_17_out, not_5_out, not_6_out);
  and and_18 (and_18_out, not_7_out, not_8_out);
  not not_17 (not_17_out, A);
  not not_18 (not_18_out, B);
  not not_19 (not_19_out, D);
  not not_20 (not_20_out, E);
  not not_21 (not_21_out, A);
  not not_22 (not_22_out, C);
  not not_23 (not_23_out, D);
  not not_24 (not_24_out, E);
  not not_25 (not_25_out, B);
  not not_26 (not_26_out, C);
  not not_27 (not_27_out, D);
  not not_28 (not_28_out, E);
  not not_29 (not_29_out, A);
  not not_30 (not_30_out, B);
  not not_31 (not_31_out, C);
  not not_32 (not_32_out, D);
  not not_33 (not_33_out, A);
  not not_34 (not_34_out, B);
  not not_35 (not_35_out, C);
  not not_36 (not_36_out, E);
  not not_37 (not_37_out, A);
  not not_38 (not_38_out, B);
  not not_39 (not_39_out, D);
  not not_40 (not_40_out, E);
  not not_41 (not_41_out, A);
  not not_42 (not_42_out, C);
  not not_43 (not_43_out, D);
  not not_44 (not_44_out, E);
  not not_45 (not_45_out, B);
  not not_46 (not_46_out, C);
  not not_47 (not_47_out, D);
  not not_48 (not_48_out, E);
  and and_19 (and_19_out, not_9_out, not_10_out);
  and and_20 (and_20_out, not_11_out, B);
  not not_49 (not_49_out, C);
  and and_21 (and_21_out, not_12_out, B);
  not not_50 (not_50_out, D);
  and and_22 (and_22_out, not_13_out, B);
  not not_51 (not_51_out, E);
  and and_23 (and_23_out, A, not_14_out);
  not not_52 (not_52_out, C);
  and and_24 (and_24_out, A, not_15_out);
  not not_53 (not_53_out, D);
  and and_25 (and_25_out, A, not_16_out);
  not not_54 (not_54_out, E);
  and and_26 (and_26_out, A, B);
  not not_55 (not_55_out, C);
  not not_56 (not_56_out, D);
  and and_27 (and_27_out, A, B);
  not not_57 (not_57_out, C);
  not not_58 (not_58_out, E);
  or or_3 (or_3_out, or_1_out, and_5_out);
  or or_4 (or_4_out, and_6_out, and_7_out);
  or or_5 (or_5_out, or_2_out, and_8_out);
  or or_6 (or_6_out, and_9_out, and_10_out);
  and and_28 (and_28_out, and_11_out, and_12_out);
  or or_7 (or_7_out, and_28_out, and_29_out);
  and and_29 (and_29_out, and_13_out, and_14_out);
  and and_30 (and_30_out, A, B);
  and and_31 (and_31_out, and_30_out, and_32_out);
  and and_32 (and_32_out, C, E);
  and and_33 (and_33_out, A, B);
  and and_34 (and_34_out, and_33_out, and_35_out);
  and and_35 (and_35_out, D, E);
  and and_36 (and_36_out, A, C);
  and and_37 (and_37_out, and_36_out, and_38_out);
  and and_38 (and_38_out, D, E);
  and and_39 (and_39_out, and_15_out, and_16_out);
  or or_8 (or_8_out, and_39_out, and_40_out);
  and and_40 (and_40_out, and_17_out, and_18_out);
  and and_41 (and_41_out, not_17_out, not_18_out);
  and and_42 (and_42_out, and_41_out, and_43_out);
  and and_43 (and_43_out, not_19_out, not_20_out);
  and and_44 (and_44_out, not_21_out, not_22_out);
  and and_45 (and_45_out, and_44_out, and_46_out);
  and and_46 (and_46_out, not_23_out, not_24_out);
  and and_47 (and_47_out, not_25_out, not_26_out);
  and and_48 (and_48_out, and_47_out, and_49_out);
  and and_49 (and_49_out, not_27_out, not_28_out);
  and and_50 (and_50_out, not_29_out, not_30_out);
  and and_51 (and_51_out, and_50_out, and_52_out);
  and and_52 (and_52_out, not_31_out, not_32_out);
  and and_53 (and_53_out, not_33_out, not_34_out);
  and and_54 (and_54_out, and_53_out, and_55_out);
  and and_55 (and_55_out, not_35_out, not_36_out);
  and and_56 (and_56_out, not_37_out, not_38_out);
  and and_57 (and_57_out, and_56_out, and_58_out);
  and and_58 (and_58_out, not_39_out, not_40_out);
  and and_59 (and_59_out, not_41_out, not_42_out);
  and and_60 (and_60_out, and_59_out, and_61_out);
  and and_61 (and_61_out, not_43_out, not_44_out);
  and and_62 (and_62_out, not_45_out, not_46_out);
  and and_63 (and_63_out, and_62_out, and_64_out);
  and and_64 (and_64_out, not_47_out, not_48_out);
  and and_65 (and_65_out, and_19_out, C);
  and and_66 (and_66_out, and_65_out, and_67_out);
  and and_67 (and_67_out, D, E);
  and and_68 (and_68_out, and_20_out, not_49_out);
  and and_69 (and_69_out, and_68_out, and_70_out);
  and and_70 (and_70_out, D, E);
  and and_71 (and_71_out, and_21_out, C);
  and and_72 (and_72_out, and_71_out, and_73_out);
  and and_73 (and_73_out, not_50_out, E);
  and and_74 (and_74_out, and_22_out, C);
  and and_75 (and_75_out, and_74_out, and_76_out);
  and and_76 (and_76_out, D, not_51_out);
  and and_77 (and_77_out, and_23_out, not_52_out);
  and and_78 (and_78_out, and_77_out, and_79_out);
  and and_79 (and_79_out, D, E);
  and and_80 (and_80_out, and_24_out, C);
  and and_81 (and_81_out, and_80_out, and_82_out);
  and and_82 (and_82_out, not_53_out, E);
  and and_83 (and_83_out, and_25_out, C);
  and and_84 (and_84_out, and_83_out, and_85_out);
  and and_85 (and_85_out, D, not_54_out);
  and and_86 (and_86_out, and_26_out, not_55_out);
  and and_87 (and_87_out, and_86_out, and_88_out);
  and and_88 (and_88_out, not_56_out, E);
  and and_89 (and_89_out, and_27_out, not_57_out);
  and and_90 (and_90_out, and_89_out, and_91_out);
  and and_91 (and_91_out, D, not_58_out);
  and and_92 (and_92_out, A, B);
  and and_93 (and_93_out, and_92_out, C);
  not not_59 (not_59_out, D);
  and and_94 (and_94_out, not_59_out, not_60_out);
  not not_60 (not_60_out, E);
  or or_9 (or_9_out, or_3_out, or_4_out);
  or or_10 (o1, or_9_out, or_11_out);
  or or_11 (or_11_out, or_5_out, or_6_out);
  or or_12 (or_12_out, or_7_out, and_31_out);
  or or_13 (or_13_out, and_34_out, and_37_out);
  or or_14 (or_14_out, or_8_out, and_42_out);
  or or_15 (or_15_out, and_45_out, and_48_out);
  or or_16 (or_16_out, and_51_out, and_54_out);
  or or_17 (or_17_out, and_57_out, and_60_out);
  or or_18 (or_18_out, and_63_out, and_66_out);
  or or_19 (or_19_out, and_69_out, and_72_out);
  or or_20 (or_20_out, and_75_out, and_78_out);
  or or_21 (or_21_out, and_81_out, and_84_out);
  or or_22 (or_22_out, and_87_out, and_90_out);
  and and_95 (and_95_out, and_93_out, and_94_out);
  or or_23 (or_23_out, or_12_out, or_13_out);
  or or_24 (or_24_out, or_14_out, or_15_out);
  or or_25 (or_25_out, or_16_out, or_17_out);
  or or_26 (or_26_out, or_18_out, or_19_out);
  or or_27 (or_27_out, or_20_out, or_21_out);
  or or_28 (or_28_out, or_22_out, and_95_out);
  or or_29 (o2, or_23_out, or_24_out);
  or or_30 (or_30_out, or_25_out, or_26_out);
  or or_31 (or_31_out, or_27_out, or_28_out);
  or or_32 (o3, or_30_out, or_31_out);
endmodule

module \задание_2_пункт2_logicfriday_о3  (
  input  A,
  input  B,
  input  C,
  input  D,
  input  E,
  output o1,
  output o2,
  output o3
);

  wire and_1_out, and_2_out, and_3_out, and_4_out, and_5_out, and_6_out, and_7_out, and_8_out, and_9_out,
       and_10_out, and_11_out, and_12_out, and_13_out, and_14_out, and_15_out, and_16_out, and_17_out,
       and_18_out, and_19_out, and_20_out, and_21_out, and_22_out, and_23_out, and_24_out, and_25_out,
       and_26_out, and_27_out, and_28_out, and_29_out, and_30_out, and_31_out, and_32_out, and_33_out,
       and_34_out, and_35_out, not_1_out, not_2_out, not_3_out, not_4_out, not_5_out, not_6_out, not_7_out,
       not_8_out, not_9_out, not_10_out, not_11_out, not_12_out, not_13_out, not_14_out, not_15_out,
       not_16_out, not_17_out, not_18_out, not_19_out, not_20_out, not_21_out, not_22_out, not_23_out,
       not_24_out, not_25_out, not_26_out, not_27_out, not_28_out, not_29_out, not_30_out, not_31_out,
       not_32_out, not_33_out, not_34_out, not_35_out, not_36_out, not_37_out, not_38_out, not_39_out,
       not_40_out, not_41_out, not_42_out, not_43_out, not_44_out, not_45_out, not_46_out, not_47_out,
       not_48_out, not_49_out, not_50_out, not_51_out, not_52_out, not_53_out, not_54_out, not_55_out,
       not_56_out, not_57_out, not_58_out, not_59_out, not_60_out;

  and and_1 (and_1_out, A, B);
  and and_2 (and_2_out, A, C);
  and and_3 (and_3_out, B, C);
  and and_4 (and_4_out, A, D);
  and and_5 (and_5_out, B, D);
  and and_6 (and_6_out, C, D);
  and and_7 (and_7_out, A, E);
  and and_8 (and_8_out, B, E);
  and and_9 (and_9_out, C, E);
  and and_10 (and_10_out, D, E);
  not not_1 (not_1_out, A);
  not not_2 (not_2_out, B);
  not not_3 (not_3_out, C);
  not not_4 (not_4_out, D);
  not not_5 (not_5_out, A);
  not not_6 (not_6_out, B);
  not not_7 (not_7_out, C);
  not not_8 (not_8_out, E);
  not not_9 (not_9_out, A);
  not not_10 (not_10_out, B);
  not not_11 (not_11_out, D);
  not not_12 (not_12_out, E);
  not not_13 (not_13_out, A);
  not not_14 (not_14_out, C);
  not not_15 (not_15_out, D);
  not not_16 (not_16_out, E);
  not not_17 (not_17_out, B);
  not not_18 (not_18_out, C);
  not not_19 (not_19_out, D);
  not not_20 (not_20_out, E);
  not not_21 (not_21_out, A);
  not not_22 (not_22_out, B);
  not not_23 (not_23_out, C);
  not not_24 (not_24_out, D);
  not not_25 (not_25_out, A);
  not not_26 (not_26_out, B);
  not not_27 (not_27_out, C);
  not not_28 (not_28_out, E);
  not not_29 (not_29_out, A);
  not not_30 (not_30_out, B);
  not not_31 (not_31_out, D);
  not not_32 (not_32_out, E);
  not not_33 (not_33_out, A);
  not not_34 (not_34_out, C);
  not not_35 (not_35_out, D);
  not not_36 (not_36_out, E);
  not not_37 (not_37_out, B);
  not not_38 (not_38_out, C);
  not not_39 (not_39_out, D);
  not not_40 (not_40_out, E);
  not not_41 (not_41_out, A);
  not not_42 (not_42_out, B);
  not not_43 (not_43_out, A);
  not not_44 (not_44_out, C);
  not not_45 (not_45_out, B);
  not not_46 (not_46_out, C);
  not not_47 (not_47_out, A);
  not not_48 (not_48_out, D);
  not not_49 (not_49_out, B);
  not not_50 (not_50_out, D);
  not not_51 (not_51_out, C);
  not not_52 (not_52_out, D);
  not not_53 (not_53_out, A);
  not not_54 (not_54_out, E);
  not not_55 (not_55_out, B);
  not not_56 (not_56_out, E);
  not not_57 (not_57_out, C);
  not not_58 (not_58_out, E);
  not not_59 (not_59_out, D);
  not not_60 (not_60_out, E);
  or or_1 (o1, and_1_out, and_2_out, and_3_out, and_4_out, and_5_out, and_6_out, and_7_out, and_8_out, and_9_out, and_10_out);
  and and_11 (and_11_out, A, B, C, D);
  and and_12 (and_12_out, not_1_out, not_2_out, not_3_out, not_4_out);
  and and_13 (and_13_out, A, B, C, E);
  and and_14 (and_14_out, A, B, D, E);
  and and_15 (and_15_out, A, C, D, E);
  and and_16 (and_16_out, B, C, D, E);
  and and_17 (and_17_out, not_5_out, not_6_out, not_7_out, not_8_out);
  and and_18 (and_18_out, not_9_out, not_10_out, not_11_out, not_12_out);
  and and_19 (and_19_out, not_13_out, not_14_out, not_15_out, not_16_out);
  and and_20 (and_20_out, not_17_out, not_18_out, not_19_out, not_20_out);
  and and_21 (and_21_out, not_21_out, not_22_out, not_23_out, not_24_out);
  and and_22 (and_22_out, not_25_out, not_26_out, not_27_out, not_28_out);
  and and_23 (and_23_out, not_29_out, not_30_out, not_31_out, not_32_out);
  and and_24 (and_24_out, not_33_out, not_34_out, not_35_out, not_36_out);
  and and_25 (and_25_out, not_37_out, not_38_out, not_39_out, not_40_out);
  and and_26 (and_26_out, not_41_out, not_42_out, C, D, E);
  and and_27 (and_27_out, not_43_out, B, not_44_out, D, E);
  and and_28 (and_28_out, A, not_45_out, not_46_out, D, E);
  and and_29 (and_29_out, not_47_out, B, C, not_48_out, E);
  and and_30 (and_30_out, A, not_49_out, C, not_50_out, E);
  and and_31 (and_31_out, A, B, not_51_out, not_52_out, E);
  and and_32 (and_32_out, not_53_out, B, C, D, not_54_out);
  and and_33 (and_33_out, A, not_55_out, C, D, not_56_out);
  and and_34 (and_34_out, A, B, not_57_out, D, not_58_out);
  and and_35 (and_35_out, A, B, C, not_59_out, not_60_out);
  or or_2 (o2, and_11_out, and_12_out, and_13_out, and_14_out, and_15_out, and_16_out, and_17_out, and_18_out, and_19_out, and_20_out);
  or or_3 (o3, and_21_out, and_22_out, and_23_out, and_24_out, and_25_out, and_26_out, and_27_out, and_28_out, and_29_out, and_30_out, and_31_out, and_32_out, and_33_out, and_34_out, and_35_out);
endmodule

module _1_1_single_output (
  input  A,
  input  B,
  input  C,
  input  D,
  input  E,
  output \output 
);

  wire and_1_out, and_2_out, and_3_out, and_4_out, and_5_out, and_6_out, and_7_out, or_1_out, or_2_out;

  and and_1 (and_1_out, B, C);
  and and_2 (and_2_out, A, C);
  and and_3 (and_3_out, A, C);
  and and_4 (and_4_out, B, D);
  and and_5 (and_5_out, and_1_out, E);
  and and_6 (and_6_out, and_2_out, E);
  and and_7 (and_7_out, and_3_out, D);
  or or_1 (or_1_out, and_4_out, and_5_out);
  or or_2 (or_2_out, and_6_out, and_7_out);
  or or_3 (\output , or_1_out, or_2_out);
endmodule

module _2_1_single_output (
  input  A,
  input  B,
  input  C,
  input  D,
  input  E,
  output \output 
);

  wire and_1_out, and_2_out, and_3_out, and_4_out, and_5_out, and_6_out, and_7_out, or_1_out, or_2_out;

  and and_1 (and_1_out, B, C);
  and and_2 (and_2_out, A, C);
  and and_3 (and_3_out, A, C);
  and and_4 (and_4_out, B, D);
  and and_5 (and_5_out, and_1_out, E);
  and and_6 (and_6_out, and_2_out, E);
  and and_7 (and_7_out, and_3_out, D);
  or or_1 (or_1_out, and_4_out, and_5_out);
  or or_2 (or_2_out, and_6_out, and_7_out);
  or or_3 (\output , or_1_out, or_2_out);
endmodule

module _1_1_so_logicfriday (
  input  A,
  input  B,
  input  C,
  input  D,
  input  E,
  output \output 
);

  wire and_1_out, and_2_out, and_3_out, and_4_out, and_5_out, and_6_out, and_7_out, or_1_out, or_2_out;

  and and_1 (and_1_out, A, C);
  and and_2 (and_2_out, A, C);
  and and_3 (and_3_out, B, C);
  and and_4 (and_4_out, B, D);
  and and_5 (and_5_out, and_1_out, D);
  and and_6 (and_6_out, and_2_out, E);
  and and_7 (and_7_out, and_3_out, E);
  or or_1 (or_1_out, and_4_out, and_5_out);
  or or_2 (or_2_out, and_6_out, and_7_out);
  or or_3 (\output , or_1_out, or_2_out);
endmodule

module _2_1_so_logicfriday (
  input  A,
  input  B,
  input  C,
  input  D,
  input  E,
  output \output 
);

  wire and_1_out, and_2_out, and_3_out, and_4_out, and_5_out, and_6_out, and_7_out, or_1_out, or_2_out;

  and and_1 (and_1_out, A, C);
  and and_2 (and_2_out, A, C);
  and and_3 (and_3_out, B, C);
  and and_4 (and_4_out, B, D);
  and and_5 (and_5_out, and_1_out, D);
  and and_6 (and_6_out, and_2_out, E);
  and and_7 (and_7_out, and_3_out, E);
  or or_1 (or_1_out, and_4_out, and_5_out);
  or or_2 (or_2_out, and_6_out, and_7_out);
  or or_3 (\output , or_1_out, or_2_out);
endmodule
