// Logisim project Лабораторная4ВС Игнатов Станислав.circ as structural Verilog: 3 circuits, main circuit main
module main (
  input  in_1,
  input  in_2,
  input  in_3,
  input  in_4,
  output out_5,
  output out_6,
  output out_7,
  output out_8
);

  nor nor_1 (out_5, in_1, out_6);
  nor nor_2 (out_6, out_5, in_2);
  nand nand_1 (out_7, in_3, out_8);
  nand nand_2 (out_8, out_7, in_4);

  // Notes on the sheet:
  //   Асинхронный RS с прямыми входами
  //   Асинхронный RS с инверсными входами
endmodule

module _2 (
  input  in_1,
  input  in_2,
  input  in_3,
  input  in_4,
  input  in_5,
  output out_6,
  output out_7,
  output out_8,
  output out_9
);

  wire nand_1_out, nand_2_out, nand_3_out, nand_4_out;

  nand nand_1 (nand_1_out, in_4, in_4);
  nand nand_2 (nand_2_out, nand_1_out, in_5);
  nand nand_3 (nand_3_out, in_1, in_2);
  nand nand_4 (nand_4_out, in_2, in_3);
  nand nand_5 (out_6, nand_3_out, out_7);
  nand nand_6 (out_7, out_6, out_6, nand_4_out);
  nand nand_7 (out_8, nand_1_out, out_9);
  nand nand_8 (out_9, out_8, nand_2_out, nand_2_out);

  // Notes on the sheet:
  //   Синхронный RS
  //   S триггер
endmodule

module _3 (
  input  in_1,
  input  in_2,
  input  in_3,
  input  in_4,
  output out_5,
  output out_6,
  output out_7,
  output out_8
);

  wire nand_1_out, nand_2_out, nand_3_out, nand_4_out, nand_5_out, nand_6_out;

  nand nand_1 (nand_1_out, in_1, nand_2_out);
  nand nand_2 (nand_2_out, in_2, in_2);
  nand nand_3 (nand_3_out, in_3, in_3);
  nand nand_4 (nand_4_out, in_4, in_4);
  nand nand_5 (nand_5_out, in_3, nand_4_out);
  nand nand_6 (nand_6_out, nand_3_out, in_4);
  nand nand_7 (out_5, nand_1_out, out_6);
  nand nand_8 (out_6, out_5, nand_2_out);
  nand nand_9 (out_7, nand_5_out, out_8);
  nand nand_10 (out_8, out_7, nand_6_out);

  // Notes on the sheet:
  //   E триггер
  //   R триггер
endmodule
